// Logisim project 单级中断.circ as structural Verilog: 9 circuits, main circuit cpu
module cpu (
);

  wire _1_out, _2_out, _3_out, alu_1_equal, \byte , clock_1_out, comparator_1_eq, compare_1_result,
       control_1_branch, \control_1_dm写入使能 , control_1_eret, \control_1_hilo写入使能 , control_1_jr,
       control_1_jump, control_1_mfc0, control_1_set, control_1_systemcall, control_1_wec0,
       \control_1_寄存器写入使能 , demultiplexer_1_out1, demultiplexer_1_out2, demultiplexer_1_out3, IE_q,
       multiplexer_1_out, nand_1_out, not_1_out, npc_1_branch_success, or_1_out, \按键采样电路_1_ir ,
       \按键采样电路_1_o1 , \按键采样电路_1_o2 , \按键采样电路_1_o3 , \继续_out , \进入中断 ;
  wire [1:0] alu_1_result, \control_1_alu_src_2位_s_ext_rfd2_s_extun_0 , control_1_op_compare,
       \control_1_寄存器写入数据选择2位_alu_dm_pc_lo , \中断号 , \中断号_2_q ;
  wire [3:0] control_1_alu_op;
  wire [4:0] control_1_ra, control_1_rb, control_1_rw, control_1_rwc0;
  wire [9:0] alu_1_result_3;
  wire [15:0] \总周期数 , \无条件分支指令数 , \有条件分支成功跳转 , \有条件分支指令数 ;
  wire [27:0] control_1_imme;
  wire [31:0] alu_1_result_2, alu_src_1_y, control_1_signed, control_1_unsigned, EPC_q, LO_q, mips_ram_1_p6,
       multiplexer_2_out, npc_1_pc_4, npc_1_pc_out, PC_q, registerfile_1_p1, registerfile_1_p7,
       registerfile_1_p8, rom_1_data, SyscallOut, \特殊寄存器_1_pc_in , \特殊寄存器_1_特殊寄存器 ;
  wire [31:12] alu_1_result_4;

  Button _1 (.out(_1_out));
  Button _2 (.out(_2_out));
  Button _3 (.out(_3_out));
  nand nand_1 (nand_1_out, control_1_systemcall, ~alu_1_equal, not_1_out);  // NAND_Gate
  Button \u_继续  (.out(\继续_out ));
  Clock clock_1 (.out(clock_1_out));
  and and_1 (\进入中断 , \按键采样电路_1_ir , IE_q);
  Multiplexer multiplexer_1 (.in0(1'b1), .in1(1'b0), .out(multiplexer_1_out), .sel(\进入中断 ));  // open: en
  or or_1 (or_1_out, \进入中断 , comparator_1_eq, control_1_eret);
  Multiplexer #(.width(32)) multiplexer_2 (
    .in0(\特殊寄存器_1_pc_in ), .in1(EPC_q), .out(multiplexer_2_out), .sel(control_1_eret));  // open: en
  not not_1 (not_1_out, \继续_out );
  Hex_Digit_Display hex_digit_display_1 (.value(SyscallOut[27:24]));  // open: dp
  Hex_Digit_Display hex_digit_display_2 (.value(SyscallOut[31:28]));  // open: dp
  LED _1_2 (.in(\按键采样电路_1_o1 ));
  \按键采样电路  \u_按键采样电路_1  (
    ._1(_1_out), ._2(_2_out), ._3(_3_out), .O1(\按键采样电路_1_o1 ), .O2(\按键采样电路_1_o2 ), .O3(\按键采样电路_1_o3 ),
    .\中断号 (\中断号 ), .IR(\按键采样电路_1_ir ), .\同步清零信号1 (demultiplexer_1_out1), .\同步清零信号2 (demultiplexer_1_out2),
    .\同步清零信号3 (demultiplexer_1_out3));
  LED _2_2 (.in(\按键采样电路_1_o2 ));
  LED _3_2 (.in(\按键采样电路_1_o3 ));
  Register #(.width(1)) IE (.D(multiplexer_1_out), .en(or_1_out), .Q(IE_q), .clk(clock_1_out));  // open: clr
  Register #(.width(32)) EPC (.D(npc_1_pc_out), .en(\进入中断 ), .Q(EPC_q), .clk(clock_1_out));  // open: clr
  Register #(.width(32)) PC (.D(multiplexer_2_out), .en(nand_1_out), .Q(PC_q), .clk(clock_1_out));  // open: clr
  Counter #(.width(16), .max('hffff)) counter_1 (
    .count(nand_1_out), .Q(\总周期数 ), .clk(clock_1_out));  // open: load, D, carry, clr
  Hex_Digit_Display hex_digit_display_3 (.value(SyscallOut[19:16]));  // open: dp
  Hex_Digit_Display hex_digit_display_4 (.value(SyscallOut[23:20]));  // open: dp
  // Probe on \中断号 
  Demultiplexer #(.select(2), .disabled(0)) demultiplexer_1 (
    .out1(demultiplexer_1_out1), .out2(demultiplexer_1_out2), .out3(demultiplexer_1_out3), .in(1'b1),
    .sel(\中断号_2_q ), .en(control_1_eret));  // open: out0
  Comparator #(.width(32), .mode("unsigned")) comparator_1 (
    .a(PC_q), .b({32{1'b0}}), .eq(comparator_1_eq));  // open: gt, lt
  Hex_Digit_Display hex_digit_display_5 (.value(SyscallOut[11:8]));  // open: dp
  Hex_Digit_Display hex_digit_display_6 (.value(SyscallOut[15:12]));  // open: dp
  Register #(.width(2)) \u_中断号_2  (.D(\中断号 ), .en(IE_q), .Q(\中断号_2_q ), .clk(clock_1_out));  // open: clr
  LED \u_中断返回  (.in(control_1_eret));
  control control_1 (
    .\寄存器写入使能 (\control_1_寄存器写入使能 ),
    .\ALU_SRC_2位_s_ext_RFD2_s_extun_0 (\control_1_alu_src_2位_s_ext_rfd2_s_extun_0 ),
    .\HILO写入使能 (\control_1_hilo写入使能 ), .OP_compare(control_1_op_compare),
    .\寄存器写入数据选择2位_alu_DM_PC_LO (\control_1_寄存器写入数据选择2位_alu_dm_pc_lo ), .JUMP(control_1_jump),
    .ALU_OP(control_1_alu_op), .Byte(\byte ), .JR(control_1_jr), .Systemcall(control_1_systemcall),
    .set(control_1_set), .\DM写入使能 (\control_1_dm写入使能 ), .Branch(control_1_branch), .CMD(rom_1_data),
    .\signed (control_1_signed), .\unsigned (control_1_unsigned), .imme(control_1_imme), .RA(control_1_ra),
    .RW(control_1_rw), .RB(control_1_rb), .ERET(control_1_eret), .RWC0(control_1_rwc0),
    .WEC0(control_1_wec0), .MFC0(control_1_mfc0));
  ROM #(.addrWidth(10), .dataWidth(32)) rom_1 (.addr(PC_q[11:2]), .data(rom_1_data));  // open: sel
  Hex_Digit_Display hex_digit_display_7 (.value(SyscallOut[7:4]));  // open: dp
  Hex_Digit_Display hex_digit_display_8 (.value(SyscallOut[3:0]));  // open: dp
  LED \u_有条件跳转成功  (.in(npc_1_branch_success));
  \分支计数  \u_分支计数_1  (
    .J(control_1_jump), .B(control_1_branch), .S(npc_1_branch_success), .T(clock_1_out), .JO(\无条件分支指令数 ),
    .BO(\有条件分支指令数 ), .JO_2(\有条件分支成功跳转 ));
  NPC npc_1 (
    .branch_success(npc_1_branch_success), ._5or16(control_1_signed), .imme(control_1_imme), .PC(PC_q),
    .BRANCH(control_1_branch), .RFD1(registerfile_1_p7), .JUMP(control_1_jump), .JR(control_1_jr),
    .compare_result(compare_1_result), .PC_out(npc_1_pc_out), .PC_4(npc_1_pc_4));
  \特殊寄存器  \u_特殊寄存器_1  (
    .\写入数据 (registerfile_1_p1), .PC(npc_1_pc_out), .T(clock_1_out), .sysout(SyscallOut),
    .PC_IN(\特殊寄存器_1_pc_in ), .WE(\control_1_寄存器写入使能 ), .RW(control_1_rw), .\进入中断 (\进入中断 ), .\中断号 (\中断号 ),
    .RFD2(registerfile_1_p8), .WEC0(control_1_wec0), .RWC0(control_1_rwc0), .\特殊寄存器 (\特殊寄存器_1_特殊寄存器 ));
  // Probe on \总周期数 
  // Probe on \无条件分支指令数 
  // Probe on \有条件分支指令数 
  // Probe on \有条件分支成功跳转 
  // Probe on control_1_rw
  // RegisterFile registerfile_1: pin names not known; wires that end beside it: registerfile_1_p1, clock_1_out, \control_1_寄存器写入使能 , control_1_rw, control_1_ra, control_1_rb, registerfile_1_p7, registerfile_1_p8
  ALU_SRC alu_src_1 (
    .\signed (control_1_signed), .RFD2(registerfile_1_p8), .\unsigned (control_1_unsigned),
    .alu_src(\control_1_alu_src_2位_s_ext_rfd2_s_extun_0 ), .MFC0(control_1_mfc0), .cp0(\特殊寄存器_1_特殊寄存器 ),
    .sys(control_1_systemcall), .Y(alu_src_1_y));
  ALU alu_1 (
    .AluOP(control_1_alu_op), .X(registerfile_1_p7), .Equal(alu_1_equal),
    .Result({alu_1_result_4, alu_1_result_3, alu_1_result}), .Y(alu_src_1_y), .Result_2(alu_1_result_2));  // open: Signed_Overflow, UnSigned_Overflow
  compare compare_1 (
    .result(compare_1_result), .choice(control_1_op_compare), .\等于 (alu_1_equal), .\小于 (alu_1_result[0]));
  Register #(.width(32)) LO (
    .D({alu_1_result_4, alu_1_result_3, alu_1_result}), .en(\control_1_hilo写入使能 ), .Q(LO_q), .clk(clock_1_out));  // open: clr
  Register #(.width(32)) HI (.D(alu_1_result_2), .en(\control_1_hilo写入使能 ), .clk(clock_1_out));  // open: Q, clr
  // MIPS_RAM mips_ram_1: pin names not known; wires that end beside it: alu_1_result_3, registerfile_1_p8, \control_1_dm写入使能 , clock_1_out, 1'b1, mips_ram_1_p6
  data_in_re data_in_re_1 (
    .result({alu_1_result_4, alu_1_result_3, alu_1_result}), .data(mips_ram_1_p6), .sel(alu_1_result),
    .PC_4(npc_1_pc_4), .\byte (\byte ), .LO(LO_q), .re_choose(\control_1_寄存器写入数据选择2位_alu_dm_pc_lo ),
    .in_8(alu_1_result[0]), .set(control_1_set), .data_in_re(registerfile_1_p1));

  // Notes on the sheet:
  //   数码管输出应该用寄存器锁存，否则显示数据只能一闪而过
  //   可以通过项目增加Logisim库的方式将前几次实验完成的电路作为子电路引入到本电路中使用
  //   指令存储器
  //   contents of rom_1 (hex, n*v repeats v):
  //   201d0100 201a33b0 201b3404 201c3458 20110001 8000c09 20110001 20120002 20130003 8000c0d 20110001
  //   20120002 20130003 8000c11 20110001 20120002 20130003 8000c15 20110001 20120002 20130003 c000d2b
  //   20100001 20110001 118fc0 112020 20020022 c 118882 12200001 8000c19 112020 20020022 c 20110001 118880
  //   112020 20020022 c 12200001 8000c23 20110001 118fc0 112020 20020022 c 1188c3 112020 20020022 c 118903
  //   112020 20020022 c 118903 112020 20020022 c 118903 112020 20020022 c 118903 112020 20020022 c 118903
  //   112020 20020022 c 118903 112020 20020022 c 118903 112020 20020022 c 20100001 109fc0 139fc3 8021
  //   2012000c 24160003 26100001 3210000f 20080008 20090001 139900 2709825 132020 20020022 c 1094022
  //   1500fff9 22100001 2018000f 2188024 108700 20080008 20090001 139902 2709825 132021 20020022 c 1094022
  //   1500fff9 108702 2c9b022 12c00001 8000c54 4020 1084027 84400 3508ffff 82021 20020022 c 2010ffff
  //   20110000 ae300000 22100001 22310004 ae300000 22100001 22310004 ae300000 22100001 22310004 ae300000
  //   22100001 22310004 ae300000 22100001 22310004 ae300000 22100001 22310004 ae300000 22100001 22310004
  //   ae300000 22100001 22310004 ae300000 22100001 22310004 ae300000 22100001 22310004 ae300000 22100001
  //   22310004 ae300000 22100001 22310004 ae300000 22100001 22310004 ae300000 22100001 22310004 ae300000
  //   22100001 22310004 ae300000 22100001 22310004 22100001 8020 2011003c 8e130000 8e340000 274402a
  //   11000002 ae330000 ae140000 2231fffc 1611fff8 102020 20020022 c 22100004 2011003c 1611fff2 20020032 c
  //   20080002 20111111 118c00 112020 20020022 c 200b001c 228001b 8812 112020 20020022 c 216bffff 1560fff9
  //   2002000a c 20090000 200b0010 34118483 20120404 118c00 129400 36318281 22520404 ad310000 2328820
  //   21290004 216bffff 1560fffb 200b0020 20090000 81310000 112020 20020022 c 21290001 216bffff 1560fff9
  //   2002000a c 2011fff1 112020 20020022 c 22310001 1a20fffb 2002000a c 23bdfffc afa40000 23bdfffc
  //   afa20000 23bdfffc afb10000 20110064 20020022 112020 c 2231ffff 1620fffc 20020032 c 8fb10000 23bd0004
  //   8fa20000 23bd0004 8fa40000 23bd0004 42000018 23bdfffc afa40000 23bdfffc afa20000 23bdfffc afb10000
  //   201100c8 20020022 112020 c 2231ffff 1620fffc 20020032 c 8fb10000 23bd0004 8fa20000 23bd0004 8fa40000
  //   23bd0004 42000018 23bdfffc afa40000 23bdfffc afa20000 23bdfffc afb10000 2011012c 20020022 112020 c
  //   2231ffff 1620fffc 20020032 c 8fb10000 23bd0004 8fa20000 23bd0004 8fa40000 23bd0004 42000018 20100000
  //   22100001 102020 20020022 c 22100002 102020 20020022 c 22100003 102020 20020022 c 22100004 102020
  //   20020022 c 22100005 102020 20020022 c 22100006 102020 20020022 c 22100007 102020 20020022 c 22100008
  //   102020 20020022 20020022 c 3e00008
  //   数码管输出
  //   寄存器文件
endmodule

module control (
  input  [31:0] CMD,
  output [31:0] \signed ,
  output [4:0] RA,
  output \HILO写入使能 ,
  output Branch,
  output [4:0] RB,
  output [31:0] \unsigned ,
  output JUMP,
  output [4:0] RW,
  output [27:0] imme,
  output JR,
  output \寄存器写入使能 ,
  output \DM写入使能 ,
  output [1:0] \寄存器写入数据选择2位_alu_DM_PC_LO ,
  output [1:0] OP_compare,
  output Byte,
  output [1:0] \ALU_SRC_2位_s_ext_RFD2_s_extun_0 ,
  output set,
  output [3:0] ALU_OP,
  output Systemcall,
  output ERET,
  output [4:0] RWC0,
  output WEC0,
  output MFC0
);

  wire ADD, ADDI, ADDIU, ADDU, AND, ANDI, BEQ, BLEZ, BNE, comparator_1_eq, comparator_2_eq, comparator_3_eq,
       comparator_4_eq, comparator_5_eq, comparator_6_eq, demultiplexer_1_out0, demultiplexer_1_out1,
       demultiplexer_1_out2, demultiplexer_1_out3, demultiplexer_1_out4, demultiplexer_1_out5,
       demultiplexer_1_out7, demultiplexer_1_out8, demultiplexer_1_out10, demultiplexer_1_out11,
       demultiplexer_1_out12, demultiplexer_1_out18, demultiplexer_1_out27, demultiplexer_2_out0,
       demultiplexer_2_out2, demultiplexer_2_out3, demultiplexer_2_out4, demultiplexer_2_out5,
       demultiplexer_2_out6, demultiplexer_2_out8, demultiplexer_2_out9, demultiplexer_2_out10,
       demultiplexer_2_out11, demultiplexer_2_out12, demultiplexer_2_out13, ext_5or16, J, JAL, LW, MFLO, NOR,
       nor_1_out, not_1_out, not_2_out, OR, or_13_out, ORI, SLL, SLT, SLTI, SLTU, SRA, SRL, SUB;
  wire [0:0] \写入寄存器选择 ;
  wire [4:0] multiplexer_2_out;
  wire [31:0] bit_extender_1_out, bit_extender_3_out, bit_extender_4_out;
  wire [31:28] shifter_1_out;

  LED led_1 (.in(J));
  LED led_2 (.in(JAL));
  LED led_3 (.in(BEQ));
  LED led_4 (.in(BNE));
  LED led_5 (.in(BLEZ));
  LED led_6 (.in(ADDI));
  LED led_7 (.in(ADDIU));
  LED led_8 (.in(SLTI));
  LED led_9 (.in(ANDI));
  LED led_10 (.in(ORI));
  LED led_11 (.in(Byte));
  LED led_12 (.in(LW));
  LED led_13 (.in(\DM写入使能 ));
  LED led_14 (.in(ERET));
  LED led_15 (.in(WEC0));
  LED led_16 (.in(MFC0));
  // Probe on \寄存器写入数据选择2位_alu_DM_PC_LO 
  // Probe on \ALU_SRC_2位_s_ext_RFD2_s_extun_0 
  // Probe on ALU_OP
  // Probe on CMD[31:26]
  // Probe on CMD[31:26]
  // Probe on CMD[5:0]
  // Probe on CMD[5:0]
  LED led_17 (.in(SLL));
  LED led_18 (.in(SRL));
  LED led_19 (.in(SRA));
  LED led_20 (.in(JR));
  LED led_21 (.in(Systemcall));
  LED led_22 (.in(MFLO));
  LED led_23 (.in(\HILO写入使能 ));
  LED led_24 (.in(ADD));
  LED led_25 (.in(ADDU));
  LED led_26 (.in(SUB));
  LED led_27 (.in(AND));
  LED led_28 (.in(OR));
  LED led_29 (.in(NOR));
  LED led_30 (.in(SLT));
  LED led_31 (.in(SLTU));
  Demultiplexer #(.select(5), .disabled(0)) demultiplexer_1 (
    .out0(demultiplexer_1_out0), .out1(demultiplexer_1_out1), .out2(demultiplexer_1_out2),
    .out3(demultiplexer_1_out3), .out4(demultiplexer_1_out4), .out5(demultiplexer_1_out5),
    .out7(demultiplexer_1_out7), .out8(demultiplexer_1_out8), .out10(demultiplexer_1_out10),
    .out11(demultiplexer_1_out11), .out12(demultiplexer_1_out12), .out18(demultiplexer_1_out18),
    .out27(demultiplexer_1_out27), .in(1'b1), .sel(CMD[4:0]));  // open: out6, out9, out13, out14, out15, out16, out17, out19, out20, out21, out22, out23, out24, out25, out26, out28, out29, out30, out31, en
  nor nor_1 (nor_1_out, CMD[26], CMD[27], CMD[28], CMD[30], CMD[31], CMD[29]);
  not not_1 (not_1_out, CMD[5]);
  Comparator #(.width(6), .mode("unsigned")) comparator_1 (
    .a(CMD[31:26]), .b(6'b010000), .eq(comparator_1_eq));  // open: gt, lt
  Comparator #(.width(5), .mode("unsigned")) comparator_2 (
    .a(CMD[25:21]), .b(5'b00100), .eq(comparator_2_eq));  // open: gt, lt
  Comparator #(.width(6), .mode("unsigned")) comparator_3 (
    .a(CMD[31:26]), .b(6'b010000), .eq(comparator_3_eq));  // open: gt, lt
  Comparator #(.width(5), .mode("unsigned")) comparator_4 (
    .a(CMD[25:21]), .b({5{1'b0}}), .eq(comparator_4_eq));  // open: gt, lt
  and and_1 (WEC0, comparator_1_eq, comparator_2_eq);
  and and_2 (MFC0, comparator_3_eq, comparator_4_eq);
  assign bit_extender_1_out = {{16{CMD[15]}}, CMD[15:0]};  // Bit_Extender bit_extender_1
  assign \unsigned  = {{16{1'b0}}, CMD[15:0]};  // Bit_Extender bit_extender_2
  assign bit_extender_3_out = {{27{1'b0}}, CMD[10:6]};  // Bit_Extender bit_extender_3
  assign bit_extender_4_out = {{6{CMD[25]}}, CMD[25:0]};  // Bit_Extender bit_extender_4
  Shifter #(.width(32)) shifter_1 (.in(bit_extender_4_out), .\dist (5'b00010), .out({shifter_1_out, imme}));
  Multiplexer #(.width(32)) multiplexer_1 (
    .in0(bit_extender_1_out), .in1(bit_extender_3_out), .out(\signed ), .sel(ext_5or16));  // open: en
  Demultiplexer #(.select(5), .disabled(0)) demultiplexer_2 (
    .out0(demultiplexer_2_out0), .out2(demultiplexer_2_out2), .out3(demultiplexer_2_out3),
    .out4(demultiplexer_2_out4), .out5(demultiplexer_2_out5), .out6(demultiplexer_2_out6),
    .out8(demultiplexer_2_out8), .out9(demultiplexer_2_out9), .out10(demultiplexer_2_out10),
    .out11(demultiplexer_2_out11), .out12(demultiplexer_2_out12), .out13(demultiplexer_2_out13), .in(1'b1),
    .sel(CMD[30:26]));  // open: out1, out7, out14, out15, out16, out17, out18, out19, out20, out21, out22, out23, out24, out25, out26, out27, out28, out29, out30, out31, en
  and _0 (SLL, demultiplexer_1_out0, nor_1_out, not_1_out);
  and _2 (SRL, demultiplexer_1_out2, nor_1_out, not_1_out);
  and _3 (SRA, demultiplexer_1_out3, nor_1_out, not_1_out);
  and _8 (JR, demultiplexer_1_out8, nor_1_out, not_1_out);
  and _12 (Systemcall, demultiplexer_1_out12, nor_1_out, not_1_out);
  and _18 (MFLO, demultiplexer_1_out18, nor_1_out, not_1_out);
  and _27 (\HILO写入使能 , demultiplexer_1_out27, nor_1_out, not_1_out);
  Comparator #(.width(6), .mode("unsigned")) comparator_5 (
    .a(CMD[31:26]), .b(6'b010000), .eq(comparator_5_eq));  // open: gt, lt
  Comparator #(.width(6), .mode("unsigned")) comparator_6 (
    .a(CMD[5:0]), .b(6'b011000), .eq(comparator_6_eq));  // open: gt, lt
  not not_2 (not_2_out, CMD[31]);
  and _32 (ADD, demultiplexer_1_out0, nor_1_out, CMD[5]);
  and _33 (ADDU, demultiplexer_1_out1, nor_1_out, CMD[5]);
  and _34 (SUB, demultiplexer_1_out2, nor_1_out, CMD[5]);
  and _36 (AND, demultiplexer_1_out4, nor_1_out, CMD[5]);
  and _37 (OR, demultiplexer_1_out5, nor_1_out, CMD[5]);
  and _39 (NOR, demultiplexer_1_out7, nor_1_out, CMD[5]);
  and _42 (SLT, demultiplexer_1_out10, nor_1_out, CMD[5]);
  and _43 (SLTU, demultiplexer_1_out11, nor_1_out, CMD[5]);
  LED SPECAIL (.in(nor_1_out));
  and and_3 (ERET, comparator_5_eq, comparator_6_eq);
  and _2_2 (J, demultiplexer_2_out2, not_2_out);
  and _3_2 (JAL, demultiplexer_2_out3, not_2_out);
  and _4 (BEQ, demultiplexer_2_out4, not_2_out);
  buf _5 (BNE, demultiplexer_2_out5);  // AND_Gate
  and _6 (BLEZ, demultiplexer_2_out6, not_2_out);
  and _8_2 (ADDI, demultiplexer_2_out8, not_2_out);
  and _9 (ADDIU, demultiplexer_2_out9, not_2_out);
  and _10 (SLTI, demultiplexer_2_out10, not_2_out);
  and _12_2 (ANDI, demultiplexer_2_out12, not_2_out);
  and _13 (ORI, demultiplexer_2_out13, not_2_out);
  and _32_2 (Byte, demultiplexer_2_out0, CMD[31]);
  and _35 (LW, demultiplexer_2_out3, CMD[31]);
  and _43_2 (\DM写入使能 , demultiplexer_2_out11, CMD[31]);
  Multiplexer #(.width(5)) multiplexer_2 (
    .in0(CMD[25:21]), .in1(CMD[20:16]), .out(multiplexer_2_out), .sel(ext_5or16));  // open: en
  Multiplexer #(.select(2), .width(5)) multiplexer_3 (
    .in0(CMD[20:16]), .in1(CMD[15:11]), .in2({5{1'b1}}), .out(RW), .sel({JAL, \写入寄存器选择 [0]}));  // open: in3, en
  Multiplexer #(.width(5)) multiplexer_4 (
    .in0(multiplexer_2_out), .in1(5'b00010), .out(RA), .sel(Systemcall));  // open: en
  or or_1 (\寄存器写入数据选择2位_alu_DM_PC_LO [1], JAL, MFLO);
  or or_2 (\寄存器写入数据选择2位_alu_DM_PC_LO [0], LW, MFLO, Byte);
  or or_3 (OP_compare[0], BNE, BLEZ);
  or or_4 (OP_compare[1], SLTI, SLTI, SLTU, BLEZ);
  or or_5 (JUMP, JR, J, JAL);
  or or_6 (Branch, BEQ, BNE, BLEZ);
  or or_7 (ext_5or16, SRL, SRA, SLL);
  or or_8 (set, SLT, SLTI, SLTU);
  or or_9 (\写入寄存器选择 [0], ADD, ADDU, AND, SLL, SRA, SRL, SUB, OR, NOR, SLT, SLTU, MFLO);
  or or_10 (\寄存器写入使能 , ADD, ADDI, ADDIU, ADDU, AND, ANDI, SLL, SRL, SRA, SUB, MFC0, ORI, NOR, LW, JAL, Byte, MFLO, SLT, OR, SLTI, SLTU);
  or or_11 (\ALU_SRC_2位_s_ext_RFD2_s_extun_0 [0], ADD, ADDU, SUB, OR, NOR, SLT, MFC0, BEQ, BNE, \HILO写入使能 , BLEZ, SLTU, AND);
  or or_12 (\ALU_SRC_2位_s_ext_RFD2_s_extun_0 [1], ANDI, ADDIU, BLEZ, ORI);
  or or_13 (or_13_out, BEQ, BNE, SLT, SLTI);
  or _0_2 (ALU_OP[0], MFC0, or_13_out, AND, ANDI, ADD, ADDI, ADDIU, \DM写入使能 , LW, NOR, SRA, Byte, BLEZ, ADDU);
  or _2_3 (ALU_OP[1], SRL, BLEZ, SUB, or_13_out, AND, ANDI);
  or _2_4 (ALU_OP[2], \HILO写入使能 , Byte, LW, \DM写入使能 , SLTU, SUB, MFC0, AND, ANDI, ADD, ADDI, ADDIU, ADDU);
  or _3_3 (ALU_OP[3], BLEZ, SLTU, or_13_out, NOR, ORI, OR);

  assign RB = CMD[20:16];
  assign RWC0 = CMD[15:11];

  // Other names for the same wires on the sheet: _28位立即数[27:0] = imme;
  //   ALU_SRC[1:0] = \ALU_SRC_2位_s_ext_RFD2_s_extun_0 ; FUNC[5:0] = CMD[5:0]; RD[4:0] = CMD[15:11];
  //   RT[4:0] = CMD[20:16]; RS[4:0] = CMD[25:21]; OP[5:0] = CMD[31:26]; EN_Register_write = \寄存器写入使能 ;
  //   Jump_register = JR; LB = Byte; DIVU = \HILO写入使能 ; LO_EN = \HILO写入使能 ; MTC0 = WEC0; OP_cmp[1:0] = OP_compare;
  //   EN_DM = \DM写入使能 ; SW = \DM写入使能 ; 写入寄存器选择[1] = JAL; 寄存器写入数据选择2位[1:0] = \寄存器写入数据选择2位_alu_DM_PC_LO ;
  //   无符号拓展数[31:0] = \unsigned ; 有符号拓展数[31:0] = \signed 

  // Notes on the sheet:
  //   输入引脚区
  //   指令观察区
  //   输出引脚区
endmodule

module NPC (
  input  [31:0] _5or16,
  input  [27:0] imme,
  input  [31:0] PC,
  input  BRANCH,
  input  [31:0] RFD1,
  input  JUMP,
  input  JR,
  input  compare_result,
  output [31:0] PC_out,
  output branch_success,
  output [31:0] PC_4
);

  wire [31:0] adder_2_out, multiplexer_1_out, multiplexer_2_out, shifter_1_out;

  Adder #(.width(32)) adder_1 (.a(32'h4), .b(PC), .out(PC_4));  // open: cin, cout
  // Probe on imme
  Multiplexer #(.width(32), .disabled(0)) multiplexer_1 (
    .in0({PC_4[31:28], imme}), .in1(RFD1), .out(multiplexer_1_out), .sel(JR));  // open: en
  Shifter #(.width(32)) shifter_1 (.in(_5or16), .\dist (5'b00010), .out(shifter_1_out));
  Adder #(.width(32)) adder_2 (.a(PC_4), .b(shifter_1_out), .out(adder_2_out));  // open: cin, cout
  and and_1 (branch_success, BRANCH, compare_result);
  Multiplexer #(.width(32), .disabled(0)) multiplexer_2 (
    .in0(PC_4), .in1(adder_2_out), .out(multiplexer_2_out), .sel(branch_success));  // open: en
  Multiplexer #(.width(32), .disabled(0)) multiplexer_3 (
    .in0(multiplexer_2_out), .in1(multiplexer_1_out), .out(PC_out), .sel(JUMP));  // open: en

  // Other names for the same wires on the sheet: branch_succeed = branch_success
endmodule

// CP
module compare (
  input  [1:0] choice,
  input  \等于 ,
  input  \小于 ,
  output result
);

  wire not_1_out, or_out;

  Multiplexer #(.select(2), .disabled(0)) multiplexer_1 (
    .in0(\等于 ), .in1(not_1_out), .in2(\小于 ), .in3(or_out), .out(result), .sel(choice));  // open: en
  not not_1 (not_1_out, \等于 );
  or \or  (or_out, \等于 , \小于 );

  // Other names for the same wires on the sheet: tunnel = \小于 ; tunnel_t = \等于 
endmodule

// RE
module data_in_re (
  input  [31:0] result,
  input  [31:0] data,
  input  [1:0] sel,
  input  [31:0] PC_4,
  input  \byte ,
  input  [31:0] LO,
  input  [1:0] re_choose,
  input  in_8,
  input  set,
  output [31:0] data_in_re
);

  wire and_1_out;
  wire [7:0] multiplexer_2_out;
  wire [31:0] bit_extender_1_out, multiplexer_1_out, multiplexer_3_out;

  Multiplexer #(.width(32)) multiplexer_1 (
    .in0(data), .in1(bit_extender_1_out), .out(multiplexer_1_out), .sel(\byte ));  // open: en
  and and_1 (and_1_out, in_8, set);
  Multiplexer #(.select(2), .width(8)) multiplexer_2 (
    .in0(data[7:0]), .in1(data[15:8]), .in2(data[23:16]), .in3(data[31:24]), .out(multiplexer_2_out),
    .sel(sel));  // open: en
  Multiplexer #(.select(2), .width(32), .disabled(0)) multiplexer_3 (
    .in0(result), .in1(multiplexer_1_out), .in2(PC_4), .in3(LO), .out(multiplexer_3_out), .sel(re_choose));  // open: en
  Multiplexer #(.width(32), .disabled(0)) multiplexer_4 (
    .in0(multiplexer_3_out), .in1(32'h1), .out(data_in_re), .sel(and_1_out));  // open: en
  assign bit_extender_1_out = {{24{multiplexer_2_out[7]}}, multiplexer_2_out};  // Bit_Extender bit_extender_1
endmodule

// 按键采样
module \按键采样电路  (
  input  _1,
  input  _2,
  input  _3,
  input  \同步清零信号1 ,
  input  \同步清零信号2 ,
  input  \同步清零信号3 ,
  output O1,
  output O2,
  output O3,
  output [1:0] \中断号 ,
  output IR
);

  wire and_1_out, and_2_out, and_3_out, clock_1_out, clock_2_out, clock_3_out, d_ff_1_q, d_ff_2_q, d_ff_3_q,
       IR1_2_q, IR1_3_q, IR1_q, or_4_out, or_5_out, or_6_out, priority_encoder_1_en_out;
  wire [1:0] priority_encoder_1_out;

  Clock clock_1 (.out(clock_1_out));
  LED \_1号中断等待指示灯  (.in(O1));
  Clock clock_2 (.out(clock_2_out));
  LED \_2号中断等待指示灯  (.in(O2));
  Clock clock_3 (.out(clock_3_out));
  LED \_3号中断等待指示灯  (.in(O3));
  D_Flip_Flop d_ff_1 (.clk(_1), .D(1'b1), .Q(d_ff_1_q), .reset(IR1_q));  // open: Qn, preset, en
  or or_1 (O1, IR1_q, d_ff_1_q);
  D_Flip_Flop d_ff_2 (.clk(_2), .D(1'b1), .Q(d_ff_2_q), .reset(IR1_2_q));  // open: Qn, preset, en
  or or_2 (O2, IR1_2_q, d_ff_2_q);
  D_Flip_Flop d_ff_3 (.clk(_3), .D(1'b1), .Q(d_ff_3_q), .reset(IR1_3_q));  // open: Qn, preset, en
  or or_3 (O3, IR1_3_q, d_ff_3_q);
  or or_4 (or_4_out, d_ff_1_q, IR1_q);
  or or_5 (or_5_out, d_ff_2_q, IR1_2_q);
  or or_6 (or_6_out, d_ff_3_q, IR1_3_q);
  LED u__1 (.in(O1));
  LED u__2 (.in(O2));
  LED u__3 (.in(O3));
  and and_1 (and_1_out, or_4_out, ~\同步清零信号1 );  // AND_Gate
  and and_2 (and_2_out, or_5_out, ~\同步清零信号2 );  // AND_Gate
  and and_3 (and_3_out, or_6_out, ~\同步清零信号3 );  // AND_Gate
  D_Flip_Flop IR1 (.clk(clock_1_out), .D(and_1_out), .Q(IR1_q));  // open: Qn, preset, en, reset
  D_Flip_Flop IR1_2 (.clk(clock_2_out), .D(and_2_out), .Q(IR1_2_q));  // open: Qn, preset, en, reset
  D_Flip_Flop IR1_3 (.clk(clock_3_out), .D(and_3_out), .Q(IR1_3_q));  // open: Qn, preset, en, reset
  Priority_Encoder #(.select(2), .disabled(0)) priority_encoder_1 (
    .in1(IR1_q), .in2(IR1_2_q), .in3(IR1_3_q), .out(priority_encoder_1_out), .gs(IR),
    .en_out(priority_encoder_1_en_out), .en_in(1'b1));  // open: in0
  // Probe on \中断号 
  Multiplexer #(.width(2)) multiplexer_1 (
    .in0(priority_encoder_1_out), .in1(2'b00), .out(\中断号 ), .sel(priority_encoder_1_en_out));  // open: en

  // Other names for the same wires on the sheet: _1号中断 = _1; _1号中断等待指示 = O1; _2号中断 = _2; _2号中断等待指示 = O2; _3号中断 = _3;
  //   _3号中断等待指示 = O3

  // Notes on the sheet:
  //   中断信号源及指示电路规范（优先级3>2>1>CPU(0）)
  //   Reset 
  //   Reset 
  //   Reset 
endmodule

module \分支计数  (
  input  J,
  input  B,
  input  S,
  input  T,
  output [15:0] JO,
  output [15:0] BO,
  output [15:0] JO_2
);

  Counter #(.width(16), .max('hffff)) counter_1 (.count(J), .Q(JO), .clk(T));  // open: load, D, carry, clr
  Counter #(.width(16), .max('hffff)) counter_2 (.count(B), .Q(BO), .clk(T));  // open: load, D, carry, clr
  Counter #(.width(16), .max('hffff)) counter_3 (.count(S), .Q(JO_2), .clk(T));  // open: load, D, carry, clr
endmodule

// SRE
module \特殊寄存器  (
  input  WEC0,
  input  WE,
  input  [4:0] RW,
  input  [31:0] \写入数据 ,
  input  [31:0] PC,
  input  \进入中断 ,
  input  [1:0] \中断号 ,
  input  [4:0] RWC0,
  input  T,
  input  [31:0] RFD2,
  output [31:0] sysout,
  output [31:0] PC_IN,
  output [31:0] \特殊寄存器 
);

  wire and_1_out, and_2_out, and_3_out, and_4_out, and_5_out, and_6_out, comparator_1_eq, comparator_2_eq,
       comparator_3_eq, comparator_4_eq, comparator_5_eq, comparator_6_eq;
  wire [1:0] multiplexer_2_out;
  wire [31:0] \_26号寄存器_q , \_27号寄存器_q , \_28号寄存器_q , EPC_q, IE_q;

  Comparator #(.width(5), .mode("unsigned")) comparator_1 (.a(RW), .b(5'b00100), .eq(comparator_1_eq));  // open: gt, lt
  and and_1 (and_1_out, comparator_1_eq, WE);
  Comparator #(.width(5), .mode("unsigned")) comparator_2 (.a(RW), .b(5'b11010), .eq(comparator_2_eq));  // open: gt, lt
  and and_2 (and_2_out, comparator_2_eq, WE);
  Comparator #(.width(5), .mode("unsigned")) comparator_3 (.a(RW), .b(5'b11011), .eq(comparator_3_eq));  // open: gt, lt
  and and_3 (and_3_out, comparator_3_eq, WE);
  Comparator #(.width(5), .mode("unsigned")) comparator_4 (.a(RW), .b(5'b11100), .eq(comparator_4_eq));  // open: gt, lt
  and and_4 (and_4_out, comparator_4_eq, WE);
  Comparator #(.width(5), .mode("unsigned")) comparator_5 (
    .a(RWC0), .b(5'b01100), .eq(comparator_5_eq));  // open: gt, lt
  and and_5 (and_5_out, comparator_5_eq, WEC0);
  Comparator #(.width(5), .mode("unsigned")) comparator_6 (
    .a(RWC0), .b(5'b01100), .eq(comparator_6_eq));  // open: gt, lt
  and and_6 (and_6_out, comparator_6_eq, WEC0);
  Register #(.width(32)) systemcall (.D(\写入数据 ), .en(and_1_out), .Q(sysout), .clk(T));  // open: clr
  Register #(.width(32)) \_26号寄存器  (.D(\写入数据 ), .en(and_2_out), .Q(\_26号寄存器_q ), .clk(T));  // open: clr
  Register #(.width(32)) \_27号寄存器  (.D(\写入数据 ), .en(and_3_out), .Q(\_27号寄存器_q ), .clk(T));  // open: clr
  Register #(.width(32)) \_28号寄存器  (.D(\写入数据 ), .en(and_4_out), .Q(\_28号寄存器_q ), .clk(T));  // open: clr
  Register #(.width(32)) EPC (.D(RFD2), .en(and_5_out), .Q(EPC_q), .clk(T));  // open: clr
  Register #(.width(32)) IE (.D(RFD2), .en(and_6_out), .Q(IE_q), .clk(T));  // open: clr
  // Probe on PC_IN
  Multiplexer #(.select(2), .width(32)) multiplexer_1 (
    .in0(PC), .in1(\_26号寄存器_q ), .in2(\_27号寄存器_q ), .in3(\_28号寄存器_q ), .out(PC_IN), .sel(multiplexer_2_out));  // open: en
  Multiplexer #(.width(2)) multiplexer_2 (.in0(2'b00), .in1(\中断号 ), .out(multiplexer_2_out), .sel(\进入中断 ));  // open: en
  Multiplexer #(.width(32)) multiplexer_3 (.in0(EPC_q), .in1(IE_q), .out(\特殊寄存器 ), .sel(comparator_6_eq));  // open: en
endmodule

// Y
module ALU_SRC (
  input  [31:0] \signed ,
  input  [31:0] RFD2,
  input  [31:0] \unsigned ,
  input  [1:0] alu_src,
  input  MFC0,
  input  [31:0] cp0,
  input  sys,
  output [31:0] Y
);

  wire [31:0] multiplexer_1_out, multiplexer_2_out;

  Multiplexer #(.select(2), .width(32)) multiplexer_1 (
    .in0(\signed ), .in1(RFD2), .in2(\unsigned ), .in3({32{1'b0}}), .out(multiplexer_1_out), .sel(alu_src));  // open: en
  Multiplexer #(.width(32)) multiplexer_2 (
    .in0(multiplexer_1_out), .in1(cp0), .out(multiplexer_2_out), .sel(MFC0));  // open: en
  Multiplexer #(.width(32)) multiplexer_3 (.in0(multiplexer_2_out), .in1(32'h22), .out(Y), .sel(sys));  // open: en
endmodule
