// Logisim project 气泡流水线.circ as structural Verilog: 15 circuits, main circuit cpu
module cpu (
);

  wire and_1_out, and_2_out, and_8_out, and_9_out, clock_1_out, compare_1_out_4, datarelation_1_bubble,
       ex_mem_1_byte_out, ex_mem_1_dm_en_out, ex_mem_1_equal, ex_mem_1_lower, ex_mem_1_set_out,
       ex_mem_1_sys_out, ex_mem_1_we_out, id_ex_1_b_out, id_ex_1_byte_out, id_ex_1_dm_en_out,
       id_ex_1_hilo_out, id_ex_1_j_out, id_ex_1_jr_out, id_ex_1_set_out, id_ex_1_sys_out, id_ex_1_we_out,
       mem_rb_1_byte_out, mem_rb_1_lower, mem_rb_1_set_out, mem_rb_1_sys_out, nand_1_out,
       npc_1_branch_success, \npc_1_跳转 , registerfile_1_p3, systemout_2_out_6, systemout_q, test_1_branch,
       test_1_byte, \test_1_dm写入使能 , \test_1_hilo写入使能 , test_1_jr, test_1_jump, test_1_set,
       test_1_systemcall, \test_1_寄存器写入使能 , \test_1_有符号拓展结果选择 , tunnel, tunnel_t, undriven, \继续_out ;
  wire [1:0] ex_mem_1_data_in_re_out, id_ex_1_alu_src_out, id_ex_1_data_in_re_out, id_ex_1_op_compare_out,
       mem_rb_1_data_in_re_out, mem_rb_1_sel_out, \test_1_alu_src_2位_s_ext_rfd2_s_extun_0 ,
       test_1_op_compare, \test_1_写入寄存器选择2位_rt_rd_31号 , \test_1_寄存器写入数据选择2位_alu_dm_pc_lo ;
  wire [3:0] id_ex_1_alu_op_out, test_1_alu_op;
  wire [4:0] decode_1_rd, decode_1_rs, decode_1_rt, ex_mem_1_rw_out, id_ex_1_rw_out, rarb_1_ra, rarb_1_rw,
       registerfile_1_p4;
  wire [5:0] decode_1_func, decode_1_op;
  wire [15:0] \总周期数 , \无条件分支指令数 , \有条件分支成功跳转 , \有条件分支指令数 ;
  wire [27:0] decode_1_immi_28, id_ex_1_imme_out;
  wire [31:0] adder_1_out, alu_1_result_2, and_3_out, and_4_out, and_5_out, and_6_out, and_7_out,
       decode_1_s_ext_5, decode_1_s_ext_16, decode_1_s_extun_16, ex_mem_1_lo_out, ex_mem_1_rdf2_out,
       ex_mem_1_result_out, id_ex_1__5or16_out, id_ex_1__16un_out, id_ex_1_rfd1_out, id_ex_1_rfd2_out,
       if_id_1_ins_out, LO_q, mem_rb_1_data_out, mem_rb_1_lo_out, mem_rb_1_result_out, mips_ram_1_p6,
       multiplexer_1_out, multiplexer_2_out, multiplexer_3_out, multiplexer_4_out, npc_1_pc_out, PC_EX,
       PC_ID, PC_IF, PC_MEM, PC_RB, registerfile_1_p1, registerfile_1_p7, registerfile_1_p8, rom_1_data,
       SyscallOut, \气泡数 ;
  wire [31:1] alu_1_result;

  Clock clock_1 (.out(clock_1_out));
  Multiplexer #(.width(32)) multiplexer_1 (
    .in0(adder_1_out), .in1(npc_1_pc_out), .out(multiplexer_1_out), .sel(\npc_1_跳转 ));  // open: en
  Register #(.width(32)) PC (.D(multiplexer_1_out), .en(and_1_out), .Q(PC_IF), .clk(clock_1_out));  // open: clr
  and and_1 (and_1_out, nand_1_out, ~datarelation_1_bubble);  // AND_Gate
  nand nand_1 (nand_1_out, and_9_out, ~\继续_out );  // NAND_Gate
  Hex_Digit_Display hex_digit_display_1 (.value(SyscallOut[31:28]));  // open: dp
  Register #(.width(1)) systemout (.D(nand_1_out), .Q(systemout_q), .clk(clock_1_out));  // open: en, clr
  Button \u_继续  (.out(\继续_out ));
  Hex_Digit_Display hex_digit_display_2 (.value(SyscallOut[23:20]));  // open: dp
  Hex_Digit_Display hex_digit_display_3 (.value(SyscallOut[27:24]));  // open: dp
  Adder #(.width(32)) adder_1 (.a(32'h4), .b(PC_IF), .out(adder_1_out));  // open: cin, cout
  Counter #(.width(16), .max('hffff)) counter_1 (.Q(\总周期数 ), .clk(and_2_out));  // open: load, D, count, carry, clr
  and and_2 (and_2_out, clock_1_out, systemout_q);
  Hex_Digit_Display hex_digit_display_4 (.value(SyscallOut[15:12]));  // open: dp
  Hex_Digit_Display hex_digit_display_5 (.value(SyscallOut[19:16]));  // open: dp
  IF_ID if_id_1 (
    .PC(PC_IF), .instrution(rom_1_data), .T(clock_1_out), .clear(\npc_1_跳转 ), .PC_out(PC_ID),
    .ins_out(if_id_1_ins_out), .pause(nand_1_out), .bubble(datarelation_1_bubble));
  ROM #(.addrWidth(10), .dataWidth(32)) rom_1 (.addr(PC_IF[11:2]), .data(rom_1_data));  // open: sel
  Hex_Digit_Display hex_digit_display_6 (.value(SyscallOut[11:8]));  // open: dp
  Hex_Digit_Display hex_digit_display_7 (.value(SyscallOut[7:4]));  // open: dp
  Decode decode_1 (
    .s_ext_16(decode_1_s_ext_16), .immi_28(decode_1_immi_28), .FUNC(decode_1_func), .OP(decode_1_op),
    .CMD(if_id_1_ins_out), .RS(decode_1_rs), .s_ext_5(decode_1_s_ext_5), .RT(decode_1_rt), .RD(decode_1_rd),
    .s_extun_16(decode_1_s_extun_16));
  Hex_Digit_Display hex_digit_display_8 (.value(SyscallOut[3:0]));  // open: dp
  test test_1 (
    .\寄存器写入使能 (\test_1_寄存器写入使能 ),
    .\ALU_SRC_2位_s_ext_RFD2_s_extun_0 (\test_1_alu_src_2位_s_ext_rfd2_s_extun_0 ),
    .\HILO写入使能 (\test_1_hilo写入使能 ), .OP_compare(test_1_op_compare),
    .\寄存器写入数据选择2位_alu_DM_PC_LO (\test_1_寄存器写入数据选择2位_alu_dm_pc_lo ), .OP(decode_1_op), .JUMP(test_1_jump),
    .ALU_OP(test_1_alu_op), .Byte(test_1_byte), .JR(test_1_jr), .\有符号拓展结果选择 (\test_1_有符号拓展结果选择 ),
    .FUNC(decode_1_func), .\写入寄存器选择2位_RT_RD_31号 (\test_1_写入寄存器选择2位_rt_rd_31号 ),
    .Systemcall(test_1_systemcall), .set(test_1_set), .\DM写入使能 (\test_1_dm写入使能 ), .Branch(test_1_branch));
  Multiplexer #(.width(32), .disabled(0)) multiplexer_2 (
    .in0(decode_1_s_ext_16), .in1(decode_1_s_ext_5), .out(multiplexer_2_out), .sel(\test_1_有符号拓展结果选择 ));  // open: en
  RARB rarb_1 (
    .RS(decode_1_rs), .RT(decode_1_rt), .RD(decode_1_rd), .re_we(\test_1_写入寄存器选择2位_rt_rd_31号 ),
    ._5or16(\test_1_有符号拓展结果选择 ), .sys(test_1_systemcall), .RA(rarb_1_ra), .RW(rarb_1_rw));
  LED \PC跳转  (.in(\npc_1_跳转 ));
  // Probe on \总周期数 
  // Probe on \无条件分支指令数 
  // Probe on \有条件分支指令数 
  // Probe on \有条件分支成功跳转 
  // Probe on \气泡数 
  // Probe on multiplexer_2_out
  // Probe on rarb_1_rw
  // Probe on PC_RB
  // Probe on registerfile_1_p1
  // Probe on PC_ID
  dataRelation datarelation_1 (
    .WE(\test_1_寄存器写入使能 ), .RW(rarb_1_rw), .RA(rarb_1_ra), .RB(decode_1_rt), .T(clock_1_out),
    .bubble(datarelation_1_bubble));
  LED \u_插入气泡  (.in(datarelation_1_bubble));
  // Probe on registerfile_1_p4
  // Probe on \总周期数 
  // Probe on and_3_out
  assign and_3_out = PC_IF & 32'hfff;  // AND_Gate and_3, 32 bits wide
  assign and_4_out = PC_ID & 32'hfff;  // AND_Gate and_4, 32 bits wide
  // Probe on and_4_out
  // Probe on and_5_out
  assign and_5_out = PC_EX & 32'hfff;  // AND_Gate and_5, 32 bits wide
  // Probe on and_6_out
  assign and_6_out = PC_MEM & 32'hfff;  // AND_Gate and_6, 32 bits wide
  assign and_7_out = PC_RB & 32'hfff;  // AND_Gate and_7, 32 bits wide
  // Probe on and_7_out
  ID_EX id_ex_1 (
    .\byte (test_1_byte), .T(clock_1_out), .clear(\npc_1_跳转 ), .DM_en(\test_1_dm写入使能 ), .set(test_1_set),
    .data_in_re(\test_1_寄存器写入数据选择2位_alu_dm_pc_lo ), .sys(test_1_systemcall), .PC(PC_ID),
    .imme(decode_1_immi_28), .alu_src(\test_1_alu_src_2位_s_ext_rfd2_s_extun_0 ), .alu_op(test_1_alu_op),
    .HILO(\test_1_hilo写入使能 ), .J(test_1_jump), .JR(test_1_jr), .B(test_1_branch),
    .op_compare(test_1_op_compare), ._5or16(multiplexer_2_out), ._16un(decode_1_s_extun_16),
    .RFD1(registerfile_1_p7), .RFD2(registerfile_1_p8), .we(\test_1_寄存器写入使能 ), .RW(rarb_1_rw),
    .byte_out(id_ex_1_byte_out), .DM_en_out(id_ex_1_dm_en_out), .set_out(id_ex_1_set_out),
    .data_in_re_out(id_ex_1_data_in_re_out), .sys_out(id_ex_1_sys_out), .PC_out(PC_EX),
    .imme_out(id_ex_1_imme_out), .alu_src_out(id_ex_1_alu_src_out), .alu_op_out(id_ex_1_alu_op_out),
    .HILO_out(id_ex_1_hilo_out), .J_out(id_ex_1_j_out), .JR_out(id_ex_1_jr_out), .B_out(id_ex_1_b_out),
    .op_compare_out(id_ex_1_op_compare_out), ._5or16_out(id_ex_1__5or16_out), ._16un_out(id_ex_1__16un_out),
    .we_out(id_ex_1_we_out), .RW_out(id_ex_1_rw_out), .pause(nand_1_out), .bubble(datarelation_1_bubble),
    .RFD1_out(id_ex_1_rfd1_out), .RFD2_out(id_ex_1_rfd2_out));
  // RegisterFile registerfile_1: pin names not known; wires that end beside it: registerfile_1_p1, clock_1_out, registerfile_1_p3, registerfile_1_p4, rarb_1_ra, decode_1_rt, registerfile_1_p7, registerfile_1_p8
  // Probe on id_ex_1_rw_out
  and and_8 (and_8_out, systemout_q, datarelation_1_bubble);
  // Probe on id_ex_1_we_out
  Multiplexer #(.select(2), .width(32), .disabled(0)) multiplexer_3 (
    .in0(id_ex_1__5or16_out), .in1(id_ex_1_rfd2_out), .in2(id_ex_1__16un_out), .in3({32{1'b0}}),
    .out(multiplexer_3_out), .sel(id_ex_1_alu_src_out));  // open: en
  Counter #(.width(32), .max('hffffffff)) counter_2 (
    .count(and_8_out), .Q(\气泡数 ), .clk(clock_1_out));  // open: load, D, carry, clr
  NPC npc_1 (
    .branch_success(npc_1_branch_success), ._5or16(id_ex_1__5or16_out), .imme(id_ex_1_imme_out), .PC(PC_EX),
    .BRANCH(id_ex_1_b_out), .JUMP(id_ex_1_j_out), .JR(id_ex_1_jr_out), .compare_result(compare_1_out_4),
    .PC_out(npc_1_pc_out), .RFD1(id_ex_1_rfd1_out), .\跳转 (\npc_1_跳转 ));
  Multiplexer #(.width(32), .disabled(0)) multiplexer_4 (
    .in0(multiplexer_3_out), .in1(32'h22), .out(multiplexer_4_out), .sel(id_ex_1_sys_out));  // open: en
  \分支计数  \u_分支计数_1  (
    .J(id_ex_1_j_out), .B(id_ex_1_b_out), .S(npc_1_branch_success), .T(clock_1_out), .JO(\无条件分支指令数 ),
    .BO(\有条件分支指令数 ), .JO_2(\有条件分支成功跳转 ));
  LED \u_有条件跳转成功  (.in(npc_1_branch_success));
  compare compare_1 (.out_4(compare_1_out_4), .choice(id_ex_1_op_compare_out), .\等于 (tunnel_t), .\小于 (tunnel));
  ALU alu_1 (
    .AluOP(id_ex_1_alu_op_out), .X(id_ex_1_rfd1_out), .Equal(tunnel_t), .Result({alu_1_result, tunnel}),
    .Y(multiplexer_4_out), .Result_2(alu_1_result_2));  // open: Signed_Overflow, UnSigned_Overflow
  // Probe on {alu_1_result, tunnel}
  Register #(.width(32), .trigger("falling")) LO (
    .D({alu_1_result, tunnel}), .en(id_ex_1_hilo_out), .Q(LO_q), .clk(clock_1_out), .clr(undriven));
  Register #(.width(32), .trigger("falling")) HI (
    .D(alu_1_result_2), .en(id_ex_1_hilo_out), .clk(clock_1_out));  // open: Q, clr
  EX_MEM ex_mem_1 (
    .T(clock_1_out), .WE(id_ex_1_we_out), .RW(id_ex_1_rw_out), .\byte (id_ex_1_byte_out),
    .DM_en(id_ex_1_dm_en_out), .set(id_ex_1_set_out), .data_in_re(id_ex_1_data_in_re_out), .PC(PC_EX),
    .sys(id_ex_1_sys_out), .in_11(tunnel_t), .in_12(tunnel), .result({alu_1_result, tunnel}),
    .RDF2(id_ex_1_rfd2_out), .LO(LO_q), .WE_out(ex_mem_1_we_out), .RW_out(ex_mem_1_rw_out),
    .byte_out(ex_mem_1_byte_out), .DM_en_out(ex_mem_1_dm_en_out), .set_out(ex_mem_1_set_out),
    .data_in_re_out(ex_mem_1_data_in_re_out), .PC_out(PC_MEM), .sys_out(ex_mem_1_sys_out),
    .equal(ex_mem_1_equal), .lower(ex_mem_1_lower), .result_out(ex_mem_1_result_out),
    .RDF2_out(ex_mem_1_rdf2_out), .LO_out(ex_mem_1_lo_out), .pause(nand_1_out));  // open: clear
  // Probe on ex_mem_1_result_out[11:2]
  // Probe on ex_mem_1_rdf2_out
  // Probe on ex_mem_1_result_out
  // Probe on ex_mem_1_rw_out
  // MIPS_RAM mips_ram_1: pin names not known; wires that end beside it: ex_mem_1_result_out[11:2], ex_mem_1_rdf2_out, ex_mem_1_dm_en_out, clock_1_out, 1'b1, mips_ram_1_p6
  MEM_RB mem_rb_1 (
    .T(clock_1_out), .sel(ex_mem_1_result_out[1:0]), .WE(ex_mem_1_we_out), .RW(ex_mem_1_rw_out),
    .\byte (ex_mem_1_byte_out), .set(ex_mem_1_set_out), .data_in_re(ex_mem_1_data_in_re_out), .PC(PC_MEM),
    .sys(ex_mem_1_sys_out), .in_11(ex_mem_1_equal), .in_12(ex_mem_1_lower), .result(ex_mem_1_result_out),
    .LO(ex_mem_1_lo_out), .sel_out(mem_rb_1_sel_out), .WE_out(registerfile_1_p3), .RW_out(registerfile_1_p4),
    .byte_out(mem_rb_1_byte_out), .set_out(mem_rb_1_set_out), .data_in_re_out(mem_rb_1_data_in_re_out),
    .PC_out(PC_RB), .sys_out(mem_rb_1_sys_out), .lower(mem_rb_1_lower), .result_out(mem_rb_1_result_out),
    .LO_out(mem_rb_1_lo_out), .data(mips_ram_1_p6), .data_out(mem_rb_1_data_out), .pause(nand_1_out));  // open: clear, equal
  and and_9 (and_9_out, ~systemout_2_out_6, mem_rb_1_sys_out);  // AND_Gate
  // Probe on mem_rb_1_result_out
  \写入寄存器数据  \u_写入寄存器数据_1  (
    .sel(mem_rb_1_sel_out), .result(mem_rb_1_result_out), .data(mem_rb_1_data_out), .pc(PC_RB),
    .lo(mem_rb_1_lo_out), .\byte (mem_rb_1_byte_out), .re_in(mem_rb_1_data_in_re_out), .in_8(mem_rb_1_lower),
    .set(mem_rb_1_set_out), .data_out(registerfile_1_p1));
  systemout systemout_2 (
    .RW(registerfile_1_p4), .WE(registerfile_1_p3), .Result(registerfile_1_p1), .T(clock_1_out),
    .out_6(systemout_2_out_6), .systemout(SyscallOut));

  // Notes on the sheet:
  //   数码管输出应该用寄存器锁存，否则显示数据只能一闪而过
  //   可以通过项目增加Logisim库的方式将前几次实验完成的电路作为子电路引入到本电路中使用
  //   指令存储器
  //   contents of rom_1 (hex, n*v repeats v):
  //   20110001 8000c05 20110001 20120002 20130003 8000c09 20110001 20120002 20130003 8000c0d 20110001
  //   20120002 20130003 8000c11 20110001 20120002 20130003 c000d27 20100001 20110001 118fc0 112020
  //   20020022 c 118882 12200001 8000c15 112020 20020022 c 20110001 118880 112020 20020022 c 12200001
  //   8000c1f 20110001 118fc0 112020 20020022 c 1188c3 112020 20020022 c 118903 112020 20020022 c 118903
  //   112020 20020022 c 118903 112020 20020022 c 118903 112020 20020022 c 118903 112020 20020022 c 118903
  //   112020 20020022 c 118903 112020 20020022 c 20100001 109fc0 139fc3 8021 2012000c 24160003 26100001
  //   3210000f 20080008 20090001 139900 2709825 132020 20020022 c 1094022 1500fff9 22100001 2018000f
  //   2188024 108700 20080008 20090001 139902 2709825 132021 20020022 c 1094022 1500fff9 108702 2c9b022
  //   12c00001 8000c50 4020 1084027 84400 3508ffff 82021 20020022 c 2010ffff 20110000 ae300000 22100001
  //   22310004 ae300000 22100001 22310004 ae300000 22100001 22310004 ae300000 22100001 22310004 ae300000
  //   22100001 22310004 ae300000 22100001 22310004 ae300000 22100001 22310004 ae300000 22100001 22310004
  //   ae300000 22100001 22310004 ae300000 22100001 22310004 ae300000 22100001 22310004 ae300000 22100001
  //   22310004 ae300000 22100001 22310004 ae300000 22100001 22310004 ae300000 22100001 22310004 ae300000
  //   22100001 22310004 22100001 8020 2011003c 8e130000 8e340000 274402a 11000002 ae330000 ae140000
  //   2231fffc 1611fff8 102020 20020022 c 22100004 2011003c 1611fff2 20020032 c 20080002 20111111 118c00
  //   112020 20020022 c 200b001c 228001b 8812 112020 20020022 c 216bffff 1560fff9 2002000a c 20090000
  //   200b0010 34118483 20120404 118c00 129400 36318281 22520404 ad310000 2328820 21290004 216bffff
  //   1560fffb 200b0020 20090000 81310000 112020 20020022 c 21290001 216bffff 1560fff9 2002000a c 2011fff1
  //   112020 20020022 c 22310001 1a20fffb 2002000a c 23bdfffc afa40000 23bdfffc afa20000 23bdfffc afb10000
  //   20110064 20020022 112020 c 2231ffff 1620fffc 20020032 c 8fb10000 23bd0004 8fa20000 23bd0004 8fa40000
  //   23bd0004 42000018 23bdfffc afa40000 23bdfffc afa20000 23bdfffc afb10000 201100c8 20020022 112020 c
  //   2231ffff 1620fffc 20020032 c 8fb10000 23bd0004 8fa20000 23bd0004 8fa40000 23bd0004 42000018 23bdfffc
  //   afa40000 23bdfffc afa20000 23bdfffc afb10000 2011012c 20020022 112020 c 2231ffff 1620fffc 20020032 c
  //   8fb10000 23bd0004 8fa20000 23bd0004 8fa40000 23bd0004 42000018 20100000 22100001 102020 20020022 c
  //   22100002 102020 20020022 c 22100003 102020 20020022 c 22100004 102020 20020022 c 22100005 102020
  //   20020022 c 22100006 102020 20020022 c 22100007 102020 20020022 c 22100008 102020 20020022 20020022 c
  //   3e00008
  //   数码管输出
  //   总复位信号应将除ROM以外所有存储组件全部清零
  //   寄存器文件
endmodule

module Decode (
  input  [31:0] CMD,
  output [31:0] s_ext_16,
  output [27:0] immi_28,
  output [5:0] FUNC,
  output [5:0] OP,
  output [4:0] RS,
  output [31:0] s_ext_5,
  output [4:0] RT,
  output [4:0] RD,
  output [31:0] s_extun_16
);

  wire [31:0] bit_extender_1_out;
  wire [31:28] shifter_1_out;

  assign bit_extender_1_out = {{6{CMD[25]}}, CMD[25:0]};  // Bit_Extender bit_extender_1
  Shifter #(.width(32)) shifter_1 (.in(bit_extender_1_out), .\dist (5'b00010), .out({shifter_1_out, immi_28}));
  assign s_ext_16 = {{16{CMD[15]}}, CMD[15:0]};  // Bit_Extender bit_extender_2
  assign s_extun_16 = {{16{1'b0}}, CMD[15:0]};  // Bit_Extender bit_extender_3
  assign s_ext_5 = {{27{1'b0}}, CMD[10:6]};  // Bit_Extender bit_extender_4

  assign FUNC = CMD[5:0];
  assign OP = CMD[31:26];
  assign RD = CMD[15:11];
  assign RS = CMD[25:21];
  assign RT = CMD[20:16];

  // Other names for the same wires on the sheet: immi[27:0] = immi_28

  // Notes on the sheet:
  //   输入引脚区
  //   输出引脚区
endmodule

// BYTE
module byte_choose (
  input  byte_en,
  input  [1:0] data,
  output [3:0] byte_choose
);

  wire and_1_out, and_2_out, and_3_out, and_4_out, not_1_out, not_2_out, not_3_out, not_4_out, not_5_out;

  not not_1 (not_1_out, byte_en);
  not not_2 (not_2_out, data[1]);
  not not_3 (not_3_out, data[0]);
  not not_4 (not_4_out, data[0]);
  not not_5 (not_5_out, data[1]);
  and and_1 (and_1_out, byte_en, not_2_out, not_3_out);
  and and_2 (and_2_out, byte_en, not_4_out, data[1]);
  and and_3 (and_3_out, byte_en, data[0], not_5_out);
  and and_4 (and_4_out, byte_en, data[0], data[1]);
  or or_1 (byte_choose[0], not_1_out, and_1_out);
  or or_2 (byte_choose[1], not_1_out, and_2_out);
  or or_3 (byte_choose[2], not_1_out, and_3_out);
  or or_4 (byte_choose[3], not_1_out, and_4_out);
  // Probe on byte_choose

  // Other names for the same wires on the sheet: BYTE = byte_en; d1 = data[0]; d0 = data[1]

  // Notes on the sheet:
  //   输入引脚区
  //   输出引脚区
endmodule

// control
module test (
  input  [5:0] OP,
  input  [5:0] FUNC,
  output \寄存器写入使能 ,
  output [1:0] \ALU_SRC_2位_s_ext_RFD2_s_extun_0 ,
  output \HILO写入使能 ,
  output [1:0] OP_compare,
  output [1:0] \寄存器写入数据选择2位_alu_DM_PC_LO ,
  output JUMP,
  output Byte,
  output \有符号拓展结果选择 ,
  output [3:0] ALU_OP,
  output JR,
  output set,
  output [1:0] \写入寄存器选择2位_RT_RD_31号 ,
  output \DM写入使能 ,
  output Branch,
  output Systemcall
);

  wire ADD, ADDI, ADDIU, ADDU, AND, ANDI, BEQ, BLEZ, BNE, demultiplexer_1_out0, demultiplexer_1_out2,
       demultiplexer_1_out3, demultiplexer_1_out4, demultiplexer_1_out5, demultiplexer_1_out6,
       demultiplexer_1_out8, demultiplexer_1_out9, demultiplexer_1_out10, demultiplexer_1_out11,
       demultiplexer_1_out12, demultiplexer_1_out13, demultiplexer_2_out0, demultiplexer_2_out1,
       demultiplexer_2_out2, demultiplexer_2_out3, demultiplexer_2_out4, demultiplexer_2_out5,
       demultiplexer_2_out7, demultiplexer_2_out8, demultiplexer_2_out10, demultiplexer_2_out11,
       demultiplexer_2_out12, demultiplexer_2_out18, demultiplexer_2_out27, J, LW, MFLO, NOR, nor_1_out,
       not_1_out, not_2_out, OR, or_13_out, ORI, SLL, SLT, SLTI, SLTU, SRA, SRL, SUB;

  // Probe on OP
  // Probe on OP
  LED led_1 (.in(J));
  LED led_2 (.in(\写入寄存器选择2位_RT_RD_31号 [1]));
  LED led_3 (.in(BEQ));
  LED led_4 (.in(BNE));
  LED led_5 (.in(BLEZ));
  LED led_6 (.in(ADDI));
  LED led_7 (.in(ADDIU));
  LED led_8 (.in(SLTI));
  LED led_9 (.in(ANDI));
  LED led_10 (.in(ORI));
  LED led_11 (.in(Byte));
  LED led_12 (.in(LW));
  LED led_13 (.in(\DM写入使能 ));
  // Probe on OP
  // Probe on FUNC
  // Probe on FUNC
  // Probe on FUNC
  LED led_14 (.in(SLL));
  LED led_15 (.in(SRL));
  LED led_16 (.in(SRA));
  LED led_17 (.in(JR));
  LED led_18 (.in(Systemcall));
  LED led_19 (.in(MFLO));
  LED led_20 (.in(\HILO写入使能 ));
  LED led_21 (.in(ADD));
  LED led_22 (.in(ADDU));
  LED led_23 (.in(SUB));
  LED led_24 (.in(AND));
  LED led_25 (.in(OR));
  LED led_26 (.in(NOR));
  LED led_27 (.in(SLT));
  LED led_28 (.in(SLTU));
  // Probe on \写入寄存器选择2位_RT_RD_31号 
  // Probe on \寄存器写入数据选择2位_alu_DM_PC_LO 
  Demultiplexer #(.select(5), .disabled(0)) demultiplexer_1 (
    .out0(demultiplexer_1_out0), .out2(demultiplexer_1_out2), .out3(demultiplexer_1_out3),
    .out4(demultiplexer_1_out4), .out5(demultiplexer_1_out5), .out6(demultiplexer_1_out6),
    .out8(demultiplexer_1_out8), .out9(demultiplexer_1_out9), .out10(demultiplexer_1_out10),
    .out11(demultiplexer_1_out11), .out12(demultiplexer_1_out12), .out13(demultiplexer_1_out13), .in(1'b1),
    .sel(OP[4:0]));  // open: out1, out7, out14, out15, out16, out17, out18, out19, out20, out21, out22, out23, out24, out25, out26, out27, out28, out29, out30, out31, en
  Demultiplexer #(.select(5), .disabled(0)) demultiplexer_2 (
    .out0(demultiplexer_2_out0), .out1(demultiplexer_2_out1), .out2(demultiplexer_2_out2),
    .out3(demultiplexer_2_out3), .out4(demultiplexer_2_out4), .out5(demultiplexer_2_out5),
    .out7(demultiplexer_2_out7), .out8(demultiplexer_2_out8), .out10(demultiplexer_2_out10),
    .out11(demultiplexer_2_out11), .out12(demultiplexer_2_out12), .out18(demultiplexer_2_out18),
    .out27(demultiplexer_2_out27), .in(1'b1), .sel(FUNC[4:0]));  // open: out6, out9, out13, out14, out15, out16, out17, out19, out20, out21, out22, out23, out24, out25, out26, out28, out29, out30, out31, en
  nor nor_1 (nor_1_out, OP[0], OP[1], OP[2], OP[4], OP[5], OP[3]);
  not not_1 (not_1_out, OP[5]);
  not not_2 (not_2_out, FUNC[5]);
  // Probe on ALU_OP
  and _2 (J, demultiplexer_1_out2, not_1_out);
  and _3 (\写入寄存器选择2位_RT_RD_31号 [1], demultiplexer_1_out3, not_1_out);
  and _4 (BEQ, demultiplexer_1_out4, not_1_out);
  buf _5 (BNE, demultiplexer_1_out5);  // AND_Gate
  and _6 (BLEZ, demultiplexer_1_out6, not_1_out);
  and _8 (ADDI, demultiplexer_1_out8, not_1_out);
  and _9 (ADDIU, demultiplexer_1_out9, not_1_out);
  and _10 (SLTI, demultiplexer_1_out10, not_1_out);
  and _12 (ANDI, demultiplexer_1_out12, not_1_out);
  and _13 (ORI, demultiplexer_1_out13, not_1_out);
  // Probe on \ALU_SRC_2位_s_ext_RFD2_s_extun_0 
  and _32 (Byte, demultiplexer_1_out0, OP[5]);
  and _35 (LW, demultiplexer_1_out3, OP[5]);
  and _43 (\DM写入使能 , demultiplexer_1_out11, OP[5]);
  and _0 (SLL, demultiplexer_2_out0, nor_1_out, not_2_out);
  and _2_2 (SRL, demultiplexer_2_out2, nor_1_out, not_2_out);
  and _3_2 (SRA, demultiplexer_2_out3, nor_1_out, not_2_out);
  and _8_2 (JR, demultiplexer_2_out8, nor_1_out, not_2_out);
  and _12_2 (Systemcall, demultiplexer_2_out12, nor_1_out, not_2_out);
  and _18 (MFLO, demultiplexer_2_out18, nor_1_out, not_2_out);
  and _27 (\HILO写入使能 , demultiplexer_2_out27, nor_1_out, not_2_out);
  and _32_2 (ADD, demultiplexer_2_out0, nor_1_out, FUNC[5]);
  and _33 (ADDU, demultiplexer_2_out1, nor_1_out, FUNC[5]);
  and _34 (SUB, demultiplexer_2_out2, nor_1_out, FUNC[5]);
  and _36 (AND, demultiplexer_2_out4, nor_1_out, FUNC[5]);
  and _37 (OR, demultiplexer_2_out5, nor_1_out, FUNC[5]);
  and _39 (NOR, demultiplexer_2_out7, nor_1_out, FUNC[5]);
  and _42 (SLT, demultiplexer_2_out10, nor_1_out, FUNC[5]);
  and _43_2 (SLTU, demultiplexer_2_out11, nor_1_out, FUNC[5]);
  LED SPECAIL (.in(nor_1_out));
  or or_1 (\寄存器写入数据选择2位_alu_DM_PC_LO [1], \写入寄存器选择2位_RT_RD_31号 [1], MFLO);
  or or_2 (\寄存器写入数据选择2位_alu_DM_PC_LO [0], LW, MFLO, Byte);
  or or_3 (OP_compare[0], BNE, BLEZ);
  or or_4 (OP_compare[1], SLTI, SLTI, SLTU, BLEZ);
  or or_5 (JUMP, JR, J, \写入寄存器选择2位_RT_RD_31号 [1]);
  or or_6 (Branch, BEQ, BNE, BLEZ);
  or or_7 (\有符号拓展结果选择 , SRL, SRA, SLL);
  or or_8 (set, SLT, SLTI, SLTU);
  or or_9 (\写入寄存器选择2位_RT_RD_31号 [0], ADD, ADDU, AND, SLL, SRA, SRL, SUB, OR, NOR, SLT, SLTU, MFLO);
  or or_10 (\寄存器写入使能 , ADD, ADDI, ADDIU, ADDU, AND, ANDI, SLL, SRL, SRA, SUB, ORI, NOR, LW, \写入寄存器选择2位_RT_RD_31号 [1], Byte, MFLO, SLT, OR, SLTI, SLTU);
  or or_11 (\ALU_SRC_2位_s_ext_RFD2_s_extun_0 [0], ADD, AND, SUB, OR, NOR, SLT, BEQ, BNE, \HILO写入使能 , BLEZ, SLTU, ADDU);
  or or_12 (\ALU_SRC_2位_s_ext_RFD2_s_extun_0 [1], ORI, ADDIU, BLEZ, ANDI);
  or or_13 (or_13_out, BEQ, BNE, SLT, SLTI);
  or _0_2 (ALU_OP[0], or_13_out, AND, ANDI, ADD, ADDI, ADDIU, ADDU, \DM写入使能 , LW, SRA, Byte, BLEZ);
  or _2_3 (ALU_OP[1], SRL, BLEZ, SUB, NOR, or_13_out, AND, ANDI);
  or _2_4 (ALU_OP[2], \HILO写入使能 , Byte, LW, \DM写入使能 , SLTU, SUB, AND, ANDI, ADD, ADDI, ADDIU, ADDU);
  or _3_3 (ALU_OP[3], BLEZ, SLTU, or_13_out, NOR, ORI, OR);

  // Other names for the same wires on the sheet: ALU_SRC[1:0] = \ALU_SRC_2位_s_ext_RFD2_s_extun_0 ;
  //   EN_Register_write = \寄存器写入使能 ; ext_5or16 = \有符号拓展结果选择 ; DIVU = \HILO写入使能 ; HILO_wirte = \HILO写入使能 ;
  //   Jump_register = JR; LB = Byte; OP_cmp[1:0] = OP_compare; EN_DM = \DM写入使能 ; SW = \DM写入使能 ;
  //   写入寄存器选择[1:0] = \写入寄存器选择2位_RT_RD_31号 ; JAL = \写入寄存器选择2位_RT_RD_31号 [1];
  //   寄存器写入数据选择2位[1:0] = \寄存器写入数据选择2位_alu_DM_PC_LO 

  // Notes on the sheet:
  //   输入引脚区
  //   指令观察区
  //   输出引脚区
endmodule

module IF_ID (
  input  [31:0] PC,
  input  [31:0] instrution,
  input  T,
  input  clear,
  input  pause,
  input  bubble,
  output [31:0] PC_out,
  output [31:0] ins_out
);

  wire and_1_out, not_1_out;
  wire [31:0] multiplexer_1_out, multiplexer_2_out;

  // Probe on PC
  Multiplexer #(.width(32)) multiplexer_1 (
    .in0(PC), .in1({32{1'b0}}), .out(multiplexer_1_out), .sel(clear));  // open: en
  Multiplexer #(.width(32)) multiplexer_2 (
    .in0(instrution), .in1({32{1'b0}}), .out(multiplexer_2_out), .sel(clear));  // open: en
  not not_1 (not_1_out, bubble);
  and and_1 (and_1_out, pause, not_1_out);
  Register #(.width(32)) register_1 (.D(multiplexer_1_out), .en(and_1_out), .Q(PC_out), .clk(T));  // open: clr
  Register #(.width(32)) register_2 (.D(multiplexer_2_out), .en(and_1_out), .Q(ins_out), .clk(T));  // open: clr
  // Probe on instrution

  // Other names for the same wires on the sheet: ins[31:0] = instrution; time = T
endmodule

module ID_EX (
  input  \byte ,
  input  T,
  input  clear,
  input  DM_en,
  input  set,
  input  [1:0] data_in_re,
  input  sys,
  input  [31:0] PC,
  input  [27:0] imme,
  input  [1:0] alu_src,
  input  [3:0] alu_op,
  input  HILO,
  input  J,
  input  JR,
  input  B,
  input  [1:0] op_compare,
  input  [31:0] _5or16,
  input  [31:0] _16un,
  input  [31:0] RFD1,
  input  [31:0] RFD2,
  input  we,
  input  [4:0] RW,
  input  pause,
  input  bubble,
  output byte_out,
  output DM_en_out,
  output set_out,
  output [1:0] data_in_re_out,
  output sys_out,
  output [31:0] PC_out,
  output [27:0] imme_out,
  output [1:0] alu_src_out,
  output [3:0] alu_op_out,
  output HILO_out,
  output J_out,
  output JR_out,
  output B_out,
  output [1:0] op_compare_out,
  output [31:0] _5or16_out,
  output [31:0] _16un_out,
  output [31:0] RFD1_out,
  output [31:0] RFD2_out,
  output we_out,
  output [4:0] RW_out
);

  wire multiplexer_1_out, multiplexer_2_out, multiplexer_3_out, multiplexer_5_out, multiplexer_10_out,
       multiplexer_11_out, multiplexer_12_out, multiplexer_13_out, multiplexer_19_out, or_1_out, undriven;
  wire [1:0] multiplexer_4_out, multiplexer_8_out, multiplexer_14_out;
  wire [3:0] multiplexer_9_out;
  wire [4:0] multiplexer_20_out;
  wire [27:0] multiplexer_7_out;
  wire [31:0] multiplexer_6_out, multiplexer_15_out, multiplexer_16_out, multiplexer_17_out,
       multiplexer_18_out;

  Multiplexer multiplexer_1 (.in0(\byte ), .in1(1'b0), .out(multiplexer_1_out), .sel(or_1_out));  // open: en
  Multiplexer multiplexer_2 (.in0(DM_en), .in1(1'b0), .out(multiplexer_2_out), .sel(or_1_out));  // open: en
  Multiplexer multiplexer_3 (.in0(set), .in1(1'b0), .out(multiplexer_3_out), .sel(or_1_out));  // open: en
  Multiplexer #(.width(2)) multiplexer_4 (
    .in0(data_in_re), .in1(2'b00), .out(multiplexer_4_out), .sel(or_1_out));  // open: en
  Multiplexer multiplexer_5 (.in0(sys), .in1(1'b0), .out(multiplexer_5_out), .sel(or_1_out));  // open: en
  Multiplexer #(.width(32)) multiplexer_6 (
    .in0(PC), .in1({32{1'b0}}), .out(multiplexer_6_out), .sel(or_1_out));  // open: en
  Multiplexer #(.width(28)) multiplexer_7 (
    .in0(imme), .in1({28{1'b0}}), .out(multiplexer_7_out), .sel(or_1_out));  // open: en
  Multiplexer #(.width(2)) multiplexer_8 (
    .in0(alu_src), .in1(2'b00), .out(multiplexer_8_out), .sel(or_1_out));  // open: en
  Multiplexer #(.width(4)) multiplexer_9 (
    .in0(alu_op), .in1(4'b0000), .out(multiplexer_9_out), .sel(or_1_out));  // open: en
  Multiplexer multiplexer_10 (.in0(HILO), .in1(1'b0), .out(multiplexer_10_out), .sel(or_1_out));  // open: en
  Multiplexer multiplexer_11 (.in0(J), .in1(1'b0), .out(multiplexer_11_out), .sel(or_1_out));  // open: en
  Multiplexer multiplexer_12 (.in0(JR), .in1(1'b0), .out(multiplexer_12_out), .sel(or_1_out));  // open: en
  Multiplexer multiplexer_13 (.in0(B), .in1(1'b0), .out(multiplexer_13_out), .sel(or_1_out));  // open: en
  Multiplexer #(.width(2)) multiplexer_14 (
    .in0(op_compare), .in1(2'b00), .out(multiplexer_14_out), .sel(or_1_out));  // open: en
  Multiplexer #(.width(32)) multiplexer_15 (
    .in0(_5or16), .in1({32{1'b0}}), .out(multiplexer_15_out), .sel(or_1_out));  // open: en
  Multiplexer #(.width(32)) multiplexer_16 (
    .in0(_16un), .in1({32{1'b0}}), .out(multiplexer_16_out), .sel(or_1_out));  // open: en
  Multiplexer #(.width(32)) multiplexer_17 (
    .in0(RFD1), .in1({32{1'b0}}), .out(multiplexer_17_out), .sel(or_1_out));  // open: en
  Multiplexer #(.width(32)) multiplexer_18 (
    .in0(RFD2), .in1({32{1'b0}}), .out(multiplexer_18_out), .sel(or_1_out));  // open: en
  Multiplexer multiplexer_19 (.in0(we), .in1(1'b0), .out(multiplexer_19_out), .sel(or_1_out));  // open: en
  Multiplexer #(.width(5)) multiplexer_20 (
    .in0(RW), .in1({5{1'b0}}), .out(multiplexer_20_out), .sel(or_1_out));  // open: en
  or or_1 (or_1_out, bubble, clear);
  Register #(.width(1)) register_1 (.D(multiplexer_1_out), .en(pause), .Q(byte_out), .clk(T), .clr(undriven));
  Register #(.width(1)) register_2 (.D(multiplexer_2_out), .en(pause), .Q(DM_en_out), .clk(T), .clr(undriven));
  Register #(.width(1)) register_3 (.D(multiplexer_3_out), .en(pause), .Q(set_out), .clk(T), .clr(undriven));
  Register #(.width(2)) register_4 (.D(multiplexer_4_out), .en(pause), .Q(data_in_re_out), .clk(T), .clr(undriven));
  Register #(.width(1)) register_5 (.D(multiplexer_5_out), .en(pause), .Q(sys_out), .clk(T), .clr(undriven));
  Register #(.width(32)) register_6 (.D(multiplexer_6_out), .en(pause), .Q(PC_out), .clk(T), .clr(undriven));
  Register #(.width(28)) register_7 (.D(multiplexer_7_out), .en(pause), .Q(imme_out), .clk(T), .clr(undriven));
  Register #(.width(2)) register_8 (.D(multiplexer_8_out), .en(pause), .Q(alu_src_out), .clk(T), .clr(undriven));
  Register #(.width(4)) register_9 (.D(multiplexer_9_out), .en(pause), .Q(alu_op_out), .clk(T), .clr(undriven));
  Register #(.width(1)) register_10 (.D(multiplexer_10_out), .en(pause), .Q(HILO_out), .clk(T), .clr(undriven));
  Register #(.width(1)) register_11 (.D(multiplexer_11_out), .en(pause), .Q(J_out), .clk(T), .clr(undriven));
  Register #(.width(1)) register_12 (.D(multiplexer_12_out), .en(pause), .Q(JR_out), .clk(T), .clr(undriven));
  Register #(.width(1)) register_13 (.D(multiplexer_13_out), .en(pause), .Q(B_out), .clk(T), .clr(undriven));
  Register #(.width(2)) register_14 (.D(multiplexer_14_out), .en(pause), .Q(op_compare_out), .clk(T), .clr(undriven));
  Register #(.width(32)) register_15 (.D(multiplexer_15_out), .en(pause), .Q(_5or16_out), .clk(T), .clr(undriven));
  Register #(.width(32)) register_16 (.D(multiplexer_16_out), .en(pause), .Q(_16un_out), .clk(T), .clr(undriven));
  Register #(.width(32)) register_17 (.D(multiplexer_17_out), .en(pause), .Q(RFD1_out), .clk(T), .clr(undriven));
  Register #(.width(32)) register_18 (.D(multiplexer_18_out), .en(pause), .Q(RFD2_out), .clk(T), .clr(undriven));
  Register #(.width(1)) register_19 (.D(multiplexer_19_out), .en(pause), .Q(we_out), .clk(T), .clr(undriven));
  Register #(.width(5)) register_20 (.D(multiplexer_20_out), .en(pause), .Q(RW_out), .clk(T), .clr(undriven));

  // Other names for the same wires on the sheet: time = T
endmodule

module NPC (
  input  [31:0] _5or16,
  input  [27:0] imme,
  input  [31:0] PC,
  input  BRANCH,
  input  [31:0] RFD1,
  input  JUMP,
  input  JR,
  input  compare_result,
  output [31:0] PC_out,
  output branch_success,
  output \跳转 
);

  wire [31:0] adder_1_out, adder_2_out, multiplexer_1_out, multiplexer_2_out, shifter_1_out;

  Adder #(.width(32)) adder_1 (.a(32'h4), .b(PC), .out(adder_1_out));  // open: cin, cout
  // Probe on imme
  Shifter #(.width(32)) shifter_1 (.in(_5or16), .\dist (5'b00010), .out(shifter_1_out));
  Multiplexer #(.width(32), .disabled(0)) multiplexer_1 (
    .in0({adder_1_out[31:28], imme}), .in1(RFD1), .out(multiplexer_1_out), .sel(JR));  // open: en
  Adder #(.width(32)) adder_2 (.a(adder_1_out), .b(shifter_1_out), .out(adder_2_out));  // open: cin, cout
  and and_1 (branch_success, BRANCH, compare_result);
  Multiplexer #(.width(32), .disabled(0)) multiplexer_2 (
    .in0(adder_1_out), .in1(adder_2_out), .out(multiplexer_2_out), .sel(branch_success));  // open: en
  Multiplexer #(.width(32), .disabled(0)) multiplexer_3 (
    .in0(multiplexer_2_out), .in1(multiplexer_1_out), .out(PC_out), .sel(JUMP));  // open: en
  or or_1 (\跳转 , JUMP, branch_success);
endmodule

module EX_MEM (
  input  T,
  input  clear,
  input  WE,
  input  [4:0] RW,
  input  \byte ,
  input  DM_en,
  input  set,
  input  [1:0] data_in_re,
  input  [31:0] PC,
  input  sys,
  input  in_11,
  input  in_12,
  input  [31:0] result,
  input  [31:0] RDF2,
  input  [31:0] LO,
  input  pause,
  output WE_out,
  output [4:0] RW_out,
  output byte_out,
  output DM_en_out,
  output set_out,
  output [1:0] data_in_re_out,
  output [31:0] PC_out,
  output sys_out,
  output equal,
  output lower,
  output [31:0] result_out,
  output [31:0] RDF2_out,
  output [31:0] LO_out
);

  Register #(.width(1)) register_1 (.D(WE), .en(pause), .Q(WE_out), .clk(T), .clr(clear));
  Register #(.width(5)) register_2 (.D(RW), .en(pause), .Q(RW_out), .clk(T), .clr(clear));
  Register #(.width(1)) register_3 (.D(\byte ), .en(pause), .Q(byte_out), .clk(T), .clr(clear));
  Register #(.width(1)) register_4 (.D(DM_en), .en(pause), .Q(DM_en_out), .clk(T), .clr(clear));
  Register #(.width(1)) register_5 (.D(set), .en(pause), .Q(set_out), .clk(T), .clr(clear));
  Register #(.width(2)) register_6 (.D(data_in_re), .en(pause), .Q(data_in_re_out), .clk(T), .clr(clear));
  Register #(.width(32)) register_7 (.D(PC), .en(pause), .Q(PC_out), .clk(T), .clr(clear));
  Register #(.width(1)) register_8 (.D(sys), .en(pause), .Q(sys_out), .clk(T), .clr(clear));
  Register #(.width(1)) register_9 (.D(in_11), .en(pause), .Q(equal), .clk(T), .clr(clear));
  Register #(.width(1)) register_10 (.D(in_12), .en(pause), .Q(lower), .clk(T), .clr(clear));
  Register #(.width(32)) register_11 (.D(result), .en(pause), .Q(result_out), .clk(T), .clr(clear));
  Register #(.width(32)) register_12 (.D(RDF2), .en(pause), .Q(RDF2_out), .clk(T), .clr(clear));
  Register #(.width(32)) register_13 (.D(LO), .en(pause), .Q(LO_out), .clk(T), .clr(clear));

  // Other names for the same wires on the sheet: time = T
endmodule

module MEM_RB (
  input  T,
  input  clear,
  input  [1:0] sel,
  input  WE,
  input  [4:0] RW,
  input  \byte ,
  input  set,
  input  [1:0] data_in_re,
  input  [31:0] PC,
  input  sys,
  input  in_11,
  input  in_12,
  input  [31:0] result,
  input  [31:0] LO,
  input  [31:0] data,
  input  pause,
  output [1:0] sel_out,
  output WE_out,
  output [4:0] RW_out,
  output byte_out,
  output set_out,
  output [1:0] data_in_re_out,
  output [31:0] PC_out,
  output sys_out,
  output equal,
  output lower,
  output [31:0] result_out,
  output [31:0] LO_out,
  output [31:0] data_out
);

  Register #(.width(2)) register_1 (.D(sel), .en(pause), .Q(sel_out), .clk(T), .clr(clear));
  Register #(.width(1)) register_2 (.D(WE), .en(pause), .Q(WE_out), .clk(T), .clr(clear));
  Register #(.width(5)) register_3 (.D(RW), .en(pause), .Q(RW_out), .clk(T), .clr(clear));
  Register #(.width(1)) register_4 (.D(\byte ), .en(pause), .Q(byte_out), .clk(T), .clr(clear));
  Register #(.width(1)) register_5 (.D(set), .en(pause), .Q(set_out), .clk(T), .clr(clear));
  Register #(.width(2)) register_6 (.D(data_in_re), .en(pause), .Q(data_in_re_out), .clk(T), .clr(clear));
  Register #(.width(32)) register_7 (.D(PC), .en(pause), .Q(PC_out), .clk(T), .clr(clear));
  Register #(.width(1)) register_8 (.D(sys), .en(pause), .Q(sys_out), .clk(T), .clr(clear));
  Register #(.width(1)) register_9 (.D(in_11), .en(pause), .Q(equal), .clk(T), .clr(clear));
  Register #(.width(1)) register_10 (.D(in_12), .en(pause), .Q(lower), .clk(T), .clr(clear));
  Register #(.width(32)) register_11 (.D(result), .en(pause), .Q(result_out), .clk(T), .clr(clear));
  Register #(.width(32)) register_12 (.D(LO), .en(pause), .Q(LO_out), .clk(T), .clr(clear));
  Register #(.width(32)) register_13 (.D(data), .en(pause), .Q(data_out), .clk(T), .clr(clear));

  // Other names for the same wires on the sheet: time = T
endmodule

// Relation
module dataRelation (
  input  WE,
  input  [4:0] RW,
  input  [4:0] RA,
  input  [4:0] RB,
  input  T,
  output bubble
);

  wire and_1_out, and_2_out, and_3_out, and_4_out, and_5_out, and_6_out, comparator_1_eq, comparator_2_eq,
       comparator_3_eq, comparator_4_eq, comparator_5_eq, comparator_6_eq, comparator_7_eq, comparator_8_eq,
       multiplexer_1_out, nand_1_out, not_1_out, not_2_out, not_3_out, not_4_out, or_1_out, or_2_out, WE1,
       WE2;
  wire [1:0] priority_encoder_1_out;
  wire [4:0] multiplexer_2_out, RW1, RW2;

  Multiplexer multiplexer_1 (.in0(WE), .in1(1'b0), .out(multiplexer_1_out), .sel(bubble));  // open: en
  Multiplexer #(.width(5)) multiplexer_2 (
    .in0(RW), .in1({5{1'b0}}), .out(multiplexer_2_out), .sel(bubble));  // open: en
  Comparator #(.width(5), .mode("unsigned")) comparator_1 (.a(RW2), .b(RA), .eq(comparator_1_eq));  // open: gt, lt
  Comparator #(.width(5), .mode("unsigned")) comparator_2 (
    .a({5{1'b0}}), .b(RA), .eq(comparator_2_eq));  // open: gt, lt
  Comparator #(.width(5), .mode("unsigned")) comparator_3 (.a(RW2), .b(RB), .eq(comparator_3_eq));  // open: gt, lt
  Comparator #(.width(5), .mode("unsigned")) comparator_4 (
    .a({5{1'b0}}), .b(RB), .eq(comparator_4_eq));  // open: gt, lt
  Comparator #(.width(5), .mode("unsigned")) comparator_5 (.a(RW1), .b(RA), .eq(comparator_5_eq));  // open: gt, lt
  Comparator #(.width(5), .mode("unsigned")) comparator_6 (
    .a({5{1'b0}}), .b(RA), .eq(comparator_6_eq));  // open: gt, lt
  Comparator #(.width(5), .mode("unsigned")) comparator_7 (.a(RW1), .b(RB), .eq(comparator_7_eq));  // open: gt, lt
  Comparator #(.width(5), .mode("unsigned")) comparator_8 (
    .a({5{1'b0}}), .b(RB), .eq(comparator_8_eq));  // open: gt, lt
  Register #(.width(1)) register_1 (.D(multiplexer_1_out), .Q(WE1), .clk(T));  // open: en, clr
  Register #(.width(5)) register_2 (.D(multiplexer_2_out), .Q(RW1), .clk(T));  // open: en, clr
  not not_1 (not_1_out, comparator_2_eq);
  not not_2 (not_2_out, comparator_4_eq);
  not not_3 (not_3_out, comparator_6_eq);
  not not_4 (not_4_out, comparator_8_eq);
  and and_1 (and_1_out, comparator_1_eq, not_1_out);
  and and_2 (and_2_out, comparator_3_eq, not_2_out);
  and and_3 (and_3_out, comparator_5_eq, not_3_out);
  or or_1 (or_1_out, and_3_out, and_4_out);
  and and_4 (and_4_out, comparator_7_eq, not_4_out);
  Register #(.width(1)) register_3 (.D(WE1), .Q(WE2), .clk(T));  // open: en, clr
  Register #(.width(5)) register_4 (.D(RW1), .Q(RW2), .clk(T));  // open: en, clr
  or or_2 (or_2_out, and_1_out, and_2_out);
  and and_5 (and_5_out, WE1, or_1_out);
  and and_6 (and_6_out, WE2, or_2_out);
  nand nand_1 (nand_1_out, and_6_out, and_5_out);
  // Probe on priority_encoder_1_out
  Priority_Encoder #(.select(2), .disabled(0)) priority_encoder_1 (
    .in0(nand_1_out), .in1(and_6_out), .in2(and_5_out), .out(priority_encoder_1_out));  // open: in3, gs, en_out, en_in
  Comparator #(.width(2), .mode("unsigned")) comparator_9 (
    .a(priority_encoder_1_out), .b(2'b00), .gt(bubble));  // open: eq, lt
endmodule

module systemout (
  input  [4:0] RW,
  input  WE,
  input  [31:0] Result,
  input  T,
  output [31:0] systemout,
  output out_6
);

  wire and_1_out, and_2_out, comparator_1_eq, comparator_2_eq;
  wire [31:0] sys_q;

  Comparator #(.width(5), .mode("unsigned")) comparator_1 (.a(RW), .b(5'b00010), .eq(comparator_1_eq));  // open: gt, lt
  and and_1 (and_1_out, comparator_1_eq, WE);
  Comparator #(.width(5), .mode("unsigned")) comparator_2 (.a(RW), .b(5'b00100), .eq(comparator_2_eq));  // open: gt, lt
  and and_2 (and_2_out, comparator_2_eq, WE);
  Register #(.width(32)) systemcall (.D(Result), .en(and_2_out), .Q(systemout), .clk(T));  // open: clr
  Register #(.width(32)) sys (.D(Result), .en(and_1_out), .Q(sys_q), .clk(T));  // open: clr
  Comparator #(.width(32), .mode("unsigned")) comparator_3 (.a(sys_q), .b(32'h22), .eq(out_6));  // open: gt, lt
endmodule

// RARW
module RARB (
  input  [4:0] RS,
  input  [4:0] RT,
  input  [4:0] RD,
  input  [1:0] re_we,
  input  _5or16,
  input  sys,
  output [4:0] RA,
  output [4:0] RW
);

  Multiplexer #(.select(2), .width(5), .disabled(0)) multiplexer_1 (
    .in0(RS), .in1(RT), .in2(5'b00010), .in3(5'b00010), .out(RA), .sel({sys, _5or16}));  // open: en
  Multiplexer #(.select(2), .width(5), .disabled(0)) multiplexer_2 (
    .in0(RT), .in1(RD), .in2({5{1'b1}}), .out(RW), .sel(re_we));  // open: in3, en
endmodule

// CP
module compare (
  input  [1:0] choice,
  input  \等于 ,
  input  \小于 ,
  output out_4
);

  wire not_1_out, or_out;

  Multiplexer #(.select(2), .disabled(0)) multiplexer_1 (
    .in0(\等于 ), .in1(not_1_out), .in2(\小于 ), .in3(or_out), .out(out_4), .sel(choice));  // open: en
  not not_1 (not_1_out, \等于 );
  or \or  (or_out, \等于 , \小于 );

  // Other names for the same wires on the sheet: tunnel = \小于 ; tunnel_t = \等于 
endmodule

// RE_data
module \写入寄存器数据  (
  input  [1:0] sel,
  input  [31:0] result,
  input  [31:0] data,
  input  [31:0] pc,
  input  [31:0] lo,
  input  \byte ,
  input  [1:0] re_in,
  input  in_8,
  input  set,
  output [31:0] data_out
);

  wire [2:2] and_1_out;
  wire [4:0] multiplexer_1_out;
  wire [31:0] adder_1_out, and_2_out, multiplexer_2_out, multiplexer_3_out, or_1_out, shifter_1_out;

  Multiplexer #(.select(2), .width(5)) multiplexer_1 (
    .in0({5{1'b0}}), .in1(5'b01000), .in2(5'b10000), .in3(5'b11000), .out(multiplexer_1_out), .sel(sel));  // open: en
  Shifter #(.width(32), .shift("lr")) shifter_1 (.in(data), .\dist (multiplexer_1_out), .out(shifter_1_out));
  Multiplexer #(.width(32)) multiplexer_2 (
    .in0(data), .in1(or_1_out), .out(multiplexer_2_out), .sel(\byte ));  // open: en
  and and_1 (and_1_out[2], in_8, set);
  assign and_2_out = shifter_1_out & 32'hff;  // AND_Gate and_2, 32 bits wide
  Multiplexer #(.width(32)) multiplexer_3 (
    .in0({32{1'b0}}), .in1(32'hffffff00), .out(multiplexer_3_out), .sel(shifter_1_out[7]));  // open: en
  assign or_1_out = and_2_out | multiplexer_3_out;  // OR_Gate or_1, 32 bits wide
  Adder #(.width(32)) adder_1 (.a(32'h4), .b(pc), .out(adder_1_out));  // open: cin, cout
  Multiplexer #(.select(3), .width(32), .disabled(0)) multiplexer_4 (
    .in0(result), .in1(multiplexer_2_out), .in2(adder_1_out), .in3(lo), .in4(32'h1), .in5(32'h1),
    .in6(32'h1), .in7(32'h1), .out(data_out), .sel({and_1_out[2], re_in}));  // open: en
endmodule

// CA
module \分支计数  (
  input  J,
  input  B,
  input  S,
  input  T,
  output [15:0] JO,
  output [15:0] BO,
  output [15:0] JO_2
);

  Counter #(.width(16), .max('hffff)) counter_1 (.count(J), .Q(JO), .clk(T));  // open: load, D, carry, clr
  Counter #(.width(16), .max('hffff)) counter_2 (.count(B), .Q(BO), .clk(T));  // open: load, D, carry, clr
  Counter #(.width(16), .max('hffff)) counter_3 (.count(S), .Q(JO_2), .clk(T));  // open: load, D, carry, clr
endmodule
