// Logisim project 理想流水线.circ as structural Verilog: 9 circuits, main circuit cpu
module cpu (
);

  wire and_1_out, and_2_out, and_5_out, clock_1_out, comparator_1_eq, ex_mem_1_byte_out, ex_mem_1_dm_en_out,
       ex_mem_1_equal, ex_mem_1_lower, ex_mem_1_set_out, ex_mem_1_sys_out, ex_mem_1_we_out, id_ex_1_b_out,
       id_ex_1_byte_out, id_ex_1_dm_en_out, id_ex_1_hilo_out, id_ex_1_j_out, id_ex_1_jr_out, id_ex_1_set_out,
       id_ex_1_sys_out, id_ex_1_we_out, mem_rb_1_byte_out, mem_rb_1_equal, mem_rb_1_lower, mem_rb_1_set_out,
       mem_rb_1_sys_out, multiplexer_7_out, nand_1_out, not_1_out, not_2_out, npc_1_branch_success, or_out,
       pause_q, registerfile_1_p3, test_1_branch, test_1_byte, \test_1_dm写入使能 , \test_1_hilo写入使能 , test_1_jr,
       test_1_jump, test_1_set, test_1_systemcall, \test_1_寄存器写入使能 , \test_1_有符号拓展结果选择 , tunnel, tunnel_t,
       \总复位_out ;
  wire [1:0] ex_mem_1_data_in_re_out, id_ex_1_alu_src_out, id_ex_1_data_in_re_out, id_ex_1_op_compare_out,
       mem_rb_1_data_in_re_out, mem_rb_1_sel_out, \test_1_alu_src_2位_s_ext_rfd2_s_extun_0 ,
       test_1_op_compare, \test_1_写入寄存器选择2位_rt_rd_31号 , \test_1_寄存器写入数据选择2位_alu_dm_pc_lo ;
  wire [2:2] and_3_out;
  wire [3:0] byte_choose_1_byte_choose, id_ex_1_alu_op_out, test_1_alu_op;
  wire [4:0] decode_1_rd, decode_1_rs, decode_1_rt, ex_mem_1_rw_out, id_ex_1_rw_out, multiplexer_2_out,
       multiplexer_3_out, multiplexer_4_out, multiplexer_8_out, registerfile_1_p4;
  wire [5:0] decode_1_func, decode_1_op;
  wire [15:0] \总周期数 , \无条件分支指令数 , \有条件分支成功跳转 , \有条件分支指令数 ;
  wire [27:0] decode_1_immi_28, id_ex_1_imme_out;
  wire [31:0] adder_1_out, adder_2_out, alu_1_result_2, and_4_out, decode_1_s_ext_5, decode_1_s_ext_16,
       decode_1_s_extun_16, ex_mem_1_lo_out, ex_mem_1_rdf2_out, ex_mem_1_result_out, id_ex_1__5or16_out,
       id_ex_1__16un_out, id_ex_1_rfd1_out, id_ex_1_rfd2_out, if_id_1_ins_out, LO_q, mem_rb_1_data_out,
       mem_rb_1_lo_out, mem_rb_1_result_out, mips_ram_1_p7, multiplexer_1_out, multiplexer_5_out,
       multiplexer_6_out, multiplexer_9_out, PC_EX, PC_ID, PC_IF, PC_MEM, PC_RB, registerfile_1_p1,
       registerfile_1_p7, registerfile_1_p8, rom_1_data, shifter_1_out, SyscallOut;
  wire [31:1] alu_1_result;

  nand nand_1 (nand_1_out, and_2_out, not_1_out);
  not not_1 (not_1_out, \总复位_out );
  Clock clock_1 (.out(clock_1_out));
  Register #(.width(32)) PC (.D(adder_1_out), .en(nand_1_out), .Q(PC_IF), .clk(clock_1_out), .clr(\总复位_out ));
  // Probe on PC_IF
  // Probe on PC_ID
  // Probe on PC_EX
  // Probe on PC_MEM
  // Probe on PC_RB
  Hex_Digit_Display hex_digit_display_1 (.value(SyscallOut[27:24]));  // open: dp
  Hex_Digit_Display hex_digit_display_2 (.value(SyscallOut[31:28]));  // open: dp
  Button \u_总复位  (.out(\总复位_out ));
  Register #(.width(1)) pause (.D(nand_1_out), .Q(pause_q), .clk(clock_1_out));  // open: en, clr
  and and_1 (and_1_out, pause_q, clock_1_out);
  Hex_Digit_Display hex_digit_display_3 (.value(SyscallOut[23:20]));  // open: dp
  Hex_Digit_Display hex_digit_display_4 (.value(SyscallOut[19:16]));  // open: dp
  Adder #(.width(32)) adder_1 (.a(32'h4), .b(PC_IF), .out(adder_1_out));  // open: cin, cout
  Counter #(.width(16), .max('hffff)) counter_1 (
    .Q(\总周期数 ), .clk(and_1_out), .clr(\总复位_out ));  // open: load, D, count, carry
  Hex_Digit_Display hex_digit_display_5 (.value(SyscallOut[11:8]));  // open: dp
  Hex_Digit_Display hex_digit_display_6 (.value(SyscallOut[15:12]));  // open: dp
  IF_ID if_id_1 (
    .PC(PC_IF), .instrution(rom_1_data), .T(clock_1_out), .PC_out(PC_ID), .ins_out(if_id_1_ins_out),
    .enable(nand_1_out));
  ROM #(.addrWidth(10), .dataWidth(32)) rom_1 (.addr(PC_IF[11:2]), .data(rom_1_data));  // open: sel
  Hex_Digit_Display hex_digit_display_7 (.value(SyscallOut[7:4]));  // open: dp
  Hex_Digit_Display hex_digit_display_8 (.value(SyscallOut[3:0]));  // open: dp
  Decode decode_1 (
    .s_ext_16(decode_1_s_ext_16), .immi_28(decode_1_immi_28), .FUNC(decode_1_func), .OP(decode_1_op),
    .CMD(if_id_1_ins_out), .RS(decode_1_rs), .s_ext_5(decode_1_s_ext_5), .RT(decode_1_rt), .RD(decode_1_rd),
    .s_extun_16(decode_1_s_extun_16));
  test test_1 (
    .\寄存器写入使能 (\test_1_寄存器写入使能 ),
    .\ALU_SRC_2位_s_ext_RFD2_s_extun_0 (\test_1_alu_src_2位_s_ext_rfd2_s_extun_0 ),
    .\HILO写入使能 (\test_1_hilo写入使能 ), .OP_compare(test_1_op_compare),
    .\寄存器写入数据选择2位_alu_DM_PC_LO (\test_1_寄存器写入数据选择2位_alu_dm_pc_lo ), .OP(decode_1_op), .JUMP(test_1_jump),
    .ALU_OP(test_1_alu_op), .Byte(test_1_byte), .JR(test_1_jr), .\有符号拓展结果选择 (\test_1_有符号拓展结果选择 ),
    .FUNC(decode_1_func), .\写入寄存器选择2位_RT_RD_31号 (\test_1_写入寄存器选择2位_rt_rd_31号 ),
    .Systemcall(test_1_systemcall), .set(test_1_set), .\DM写入使能 (\test_1_dm写入使能 ), .Branch(test_1_branch));
  Multiplexer #(.width(32), .disabled(0)) multiplexer_1 (
    .in0(decode_1_s_ext_16), .in1(decode_1_s_ext_5), .out(multiplexer_1_out), .sel(\test_1_有符号拓展结果选择 ));  // open: en
  Multiplexer #(.width(5), .disabled(0)) multiplexer_2 (
    .in0(decode_1_rs), .in1(decode_1_rt), .out(multiplexer_2_out), .sel(\test_1_有符号拓展结果选择 ));  // open: en
  // Probe on \总周期数 
  // Probe on \无条件分支指令数 
  // Probe on \有条件分支指令数 
  // Probe on \有条件分支成功跳转 
  Multiplexer #(.width(5), .disabled(0)) multiplexer_3 (
    .in0(multiplexer_2_out), .in1(5'b00010), .out(multiplexer_3_out), .sel(test_1_systemcall));  // open: en
  Multiplexer #(.select(2), .width(5), .disabled(0)) multiplexer_4 (
    .in0(decode_1_rt), .in1(decode_1_rd), .in3({5{1'b1}}), .out(multiplexer_4_out),
    .sel(\test_1_写入寄存器选择2位_rt_rd_31号 ));  // open: in2, en
  // Probe on multiplexer_4_out
  // Probe on registerfile_1_p4
  ID_EX id_ex_1 (
    .\byte (test_1_byte), .T(clock_1_out), .DM_en(\test_1_dm写入使能 ), .set(test_1_set),
    .data_in_re(\test_1_寄存器写入数据选择2位_alu_dm_pc_lo ), .sys(test_1_systemcall), .PC(PC_ID),
    .imme(decode_1_immi_28), .alu_src(\test_1_alu_src_2位_s_ext_rfd2_s_extun_0 ), .alu_op(test_1_alu_op),
    .HILO(\test_1_hilo写入使能 ), .J(test_1_jump), .JR(test_1_jr), .B(test_1_branch),
    .op_compare(test_1_op_compare), .byte_out(id_ex_1_byte_out), .DM_en_out(id_ex_1_dm_en_out),
    .set_out(id_ex_1_set_out), .data_in_re_out(id_ex_1_data_in_re_out), .sys_out(id_ex_1_sys_out),
    .PC_out(PC_EX), .imme_out(id_ex_1_imme_out), .alu_src_out(id_ex_1_alu_src_out),
    .alu_op_out(id_ex_1_alu_op_out), .HILO_out(id_ex_1_hilo_out), .J_out(id_ex_1_j_out),
    .JR_out(id_ex_1_jr_out), .B_out(id_ex_1_b_out), .op_compare_out(id_ex_1_op_compare_out),
    ._5or16(multiplexer_1_out), ._16un(decode_1_s_extun_16), ._5or16_out(id_ex_1__5or16_out),
    ._16un_out(id_ex_1__16un_out), .RFD1(registerfile_1_p7), .RFD2(registerfile_1_p8),
    .RFD2_out(id_ex_1_rfd2_out), .RFD1_out(id_ex_1_rfd1_out), .we(\test_1_寄存器写入使能 ), .we_out(id_ex_1_we_out),
    .RW(multiplexer_4_out), .RW_out(id_ex_1_rw_out), .enable(nand_1_out));
  // RegisterFile registerfile_1: pin names not known; wires that end beside it: registerfile_1_p1, clock_1_out, registerfile_1_p3, registerfile_1_p4, multiplexer_3_out, decode_1_rt, registerfile_1_p7, registerfile_1_p8
  // Probe on id_ex_1_rw_out
  // Probe on id_ex_1_we_out
  Multiplexer #(.select(2), .width(32), .disabled(0)) multiplexer_5 (
    .in0(id_ex_1__5or16_out), .in1(id_ex_1_rfd2_out), .in2(id_ex_1__16un_out), .in3({32{1'b0}}),
    .out(multiplexer_5_out), .sel(id_ex_1_alu_src_out));  // open: en
  NPC npc_1 (
    .branch_success(npc_1_branch_success), ._5or16(id_ex_1__5or16_out), .imme(id_ex_1_imme_out), .PC(PC_EX),
    .BRANCH(id_ex_1_b_out), .JUMP(id_ex_1_j_out), .JR(id_ex_1_jr_out), .compare_result(multiplexer_7_out),
    .RFD1(id_ex_1_rfd1_out));  // open: PC_out
  Multiplexer #(.width(32), .disabled(0)) multiplexer_6 (
    .in0(multiplexer_5_out), .in1(32'ha), .out(multiplexer_6_out), .sel(id_ex_1_sys_out));  // open: en
  Multiplexer #(.select(2), .disabled(0)) multiplexer_7 (
    .in0(tunnel_t), .in1(not_2_out), .in2(tunnel), .in3(or_out), .out(multiplexer_7_out),
    .sel(id_ex_1_op_compare_out));  // open: en
  Counter #(.width(16), .max('hffff)) counter_2 (
    .count(id_ex_1_j_out), .Q(\无条件分支指令数 ), .clk(clock_1_out));  // open: load, D, carry, clr
  Counter #(.width(16), .max('hffff)) counter_3 (
    .count(id_ex_1_b_out), .Q(\有条件分支指令数 ), .clk(clock_1_out));  // open: load, D, carry, clr
  Counter #(.width(16), .max('hffff)) counter_4 (
    .count(npc_1_branch_success), .Q(\有条件分支成功跳转 ), .clk(clock_1_out));  // open: load, D, carry, clr
  LED \u_有条件跳转成功  (.in(npc_1_branch_success));
  not not_2 (not_2_out, tunnel_t);
  or \or  (or_out, tunnel_t, tunnel);
  ALU alu_1 (
    .AluOP(id_ex_1_alu_op_out), .X(id_ex_1_rfd1_out), .Equal(tunnel_t), .Result({alu_1_result, tunnel}),
    .Y(multiplexer_6_out), .Result_2(alu_1_result_2));  // open: Signed_Overflow, UnSigned_Overflow
  EX_MEM ex_mem_1 (
    .T(clock_1_out), .WE(id_ex_1_we_out), .RW(id_ex_1_rw_out), .\byte (id_ex_1_byte_out),
    .DM_en(id_ex_1_dm_en_out), .set(id_ex_1_set_out), .data_in_re(id_ex_1_data_in_re_out), .PC(PC_EX),
    .sys(id_ex_1_sys_out), .in_4(tunnel_t), .in_6(tunnel), .result({alu_1_result, tunnel}),
    .RDF2(id_ex_1_rfd2_out), .LO(LO_q), .WE_out(ex_mem_1_we_out), .RW_out(ex_mem_1_rw_out),
    .byte_out(ex_mem_1_byte_out), .DM_en_out(ex_mem_1_dm_en_out), .set_out(ex_mem_1_set_out),
    .data_in_re_out(ex_mem_1_data_in_re_out), .PC_out(PC_MEM), .sys_out(ex_mem_1_sys_out),
    .equal(ex_mem_1_equal), .lower(ex_mem_1_lower), .result_out(ex_mem_1_result_out),
    .RDF2_out(ex_mem_1_rdf2_out), .LO_out(ex_mem_1_lo_out), .enable(nand_1_out));
  Register #(.width(32)) LO (
    .D({alu_1_result, tunnel}), .en(id_ex_1_hilo_out), .Q(LO_q), .clk(clock_1_out), .clr(clock_1_out));
  Register #(.width(32)) HI (
    .D(alu_1_result_2), .en(id_ex_1_hilo_out), .clk(clock_1_out), .clr(clock_1_out));  // open: Q
  // Probe on ex_mem_1_rdf2_out
  // Probe on ex_mem_1_result_out[11:2]
  byte_choose byte_choose_1 (
    .byte_en(ex_mem_1_byte_out), .byte_choose(byte_choose_1_byte_choose), .data(ex_mem_1_result_out[1:0]));
  // MIPS_RAM mips_ram_1: pin names not known; wires that end beside it: ex_mem_1_result_out[11:2], ex_mem_1_rdf2_out, ex_mem_1_dm_en_out, byte_choose_1_byte_choose, clock_1_out, 1'b1, mips_ram_1_p7
  MEM_RB mem_rb_1 (
    .T(clock_1_out), .sel(ex_mem_1_result_out[1:0]), .WE(ex_mem_1_we_out), .RW(ex_mem_1_rw_out),
    .\byte (ex_mem_1_byte_out), .set(ex_mem_1_set_out), .data_in_re(ex_mem_1_data_in_re_out), .PC(PC_MEM),
    .sys(ex_mem_1_sys_out), .in_4(ex_mem_1_equal), .in_6(ex_mem_1_lower), .result(ex_mem_1_result_out),
    .LO(ex_mem_1_lo_out), .sel_out(mem_rb_1_sel_out), .WE_out(registerfile_1_p3), .RW_out(registerfile_1_p4),
    .byte_out(mem_rb_1_byte_out), .set_out(mem_rb_1_set_out), .data_in_re_out(mem_rb_1_data_in_re_out),
    .PC_out(PC_RB), .sys_out(mem_rb_1_sys_out), .equal(mem_rb_1_equal), .lower(mem_rb_1_lower),
    .result_out(mem_rb_1_result_out), .LO_out(mem_rb_1_lo_out), .data(mips_ram_1_p7),
    .data_out(mem_rb_1_data_out), .in_14(nand_1_out));
  and and_2 (and_2_out, mem_rb_1_equal, mem_rb_1_sys_out);
  Multiplexer #(.select(2), .width(5)) multiplexer_8 (
    .in0({5{1'b0}}), .in1(5'b01000), .in2(5'b10000), .in3(5'b11000), .out(multiplexer_8_out),
    .sel(mem_rb_1_sel_out));  // open: en
  Multiplexer #(.width(32)) multiplexer_9 (
    .in0(mem_rb_1_data_out), .in1(and_4_out), .out(multiplexer_9_out), .sel(mem_rb_1_byte_out));  // open: en
  and and_3 (and_3_out[2], mem_rb_1_lower, mem_rb_1_set_out);
  Shifter #(.width(32), .shift("lr")) shifter_1 (
    .in(mem_rb_1_data_out), .\dist (multiplexer_8_out), .out(shifter_1_out));
  assign and_4_out = shifter_1_out & 32'hff;  // AND_Gate and_4, 32 bits wide
  Adder #(.width(32)) adder_2 (.a(32'h4), .b(PC_RB), .out(adder_2_out));  // open: cin, cout
  Multiplexer #(.select(3), .width(32), .disabled(0)) multiplexer_10 (
    .in0(mem_rb_1_result_out), .in1(multiplexer_9_out), .in2(adder_2_out), .in3(mem_rb_1_lo_out),
    .in4(32'h1), .out(registerfile_1_p1), .sel({and_3_out[2], mem_rb_1_data_in_re_out}));  // open: in5, in6, in7, en
  Comparator #(.width(5), .mode("unsigned")) comparator_1 (
    .a(registerfile_1_p4), .b(5'b00100), .eq(comparator_1_eq));  // open: gt, lt
  and and_5 (and_5_out, comparator_1_eq, registerfile_1_p3);
  Register #(.width(32)) systemcall (
    .D(registerfile_1_p1), .en(and_5_out), .Q(SyscallOut), .clk(clock_1_out));  // open: clr

  // Notes on the sheet:
  //   数码管输出应该用寄存器锁存，否则显示数据只能一闪而过
  //   可以通过项目增加Logisim库的方式将前几次实验完成的电路作为子电路引入到本电路中使用
  //   指令存储器
  //   contents of rom_1 (hex, n*v repeats v):
  //   20100000 20110000 20120000 20130000 36100000 36310001 36520002 36730003 ae100000 ae110004 ae120008
  //   ae13000c 2002000a 20110000 20120000 20130000 c
  //   数码管输出
  //   总复位信号应将除ROM以外所有存储组件全部清零
  //   寄存器文件
endmodule

module Decode (
  input  [31:0] CMD,
  output [31:0] s_ext_16,
  output [27:0] immi_28,
  output [5:0] FUNC,
  output [5:0] OP,
  output [4:0] RS,
  output [31:0] s_ext_5,
  output [4:0] RT,
  output [4:0] RD,
  output [31:0] s_extun_16
);

  wire [31:0] bit_extender_1_out;
  wire [31:28] shifter_1_out;

  assign bit_extender_1_out = {{6{CMD[25]}}, CMD[25:0]};  // Bit_Extender bit_extender_1
  Shifter #(.width(32)) shifter_1 (.in(bit_extender_1_out), .\dist (5'b00010), .out({shifter_1_out, immi_28}));
  assign s_ext_16 = {{16{CMD[15]}}, CMD[15:0]};  // Bit_Extender bit_extender_2
  assign s_extun_16 = {{16{1'b0}}, CMD[15:0]};  // Bit_Extender bit_extender_3
  assign s_ext_5 = {{27{1'b0}}, CMD[10:6]};  // Bit_Extender bit_extender_4

  assign FUNC = CMD[5:0];
  assign OP = CMD[31:26];
  assign RD = CMD[15:11];
  assign RS = CMD[25:21];
  assign RT = CMD[20:16];

  // Other names for the same wires on the sheet: immi[27:0] = immi_28

  // Notes on the sheet:
  //   输入引脚区
  //   输出引脚区
endmodule

// BYTE
module byte_choose (
  input  byte_en,
  input  [1:0] data,
  output [3:0] byte_choose
);

  wire and_1_out, and_2_out, and_3_out, and_4_out, not_1_out, not_2_out, not_3_out, not_4_out, not_5_out;

  not not_1 (not_1_out, byte_en);
  not not_2 (not_2_out, data[1]);
  not not_3 (not_3_out, data[0]);
  not not_4 (not_4_out, data[0]);
  not not_5 (not_5_out, data[1]);
  and and_1 (and_1_out, byte_en, not_2_out, not_3_out);
  and and_2 (and_2_out, byte_en, not_4_out, data[1]);
  and and_3 (and_3_out, byte_en, data[0], not_5_out);
  and and_4 (and_4_out, byte_en, data[0], data[1]);
  or or_1 (byte_choose[0], not_1_out, and_1_out);
  or or_2 (byte_choose[1], not_1_out, and_2_out);
  or or_3 (byte_choose[2], not_1_out, and_3_out);
  or or_4 (byte_choose[3], not_1_out, and_4_out);
  // Probe on byte_choose

  // Other names for the same wires on the sheet: BYTE = byte_en; d1 = data[0]; d0 = data[1]

  // Notes on the sheet:
  //   输入引脚区
  //   输出引脚区
endmodule

// control
module test (
  input  [5:0] OP,
  input  [5:0] FUNC,
  output \寄存器写入使能 ,
  output [1:0] \ALU_SRC_2位_s_ext_RFD2_s_extun_0 ,
  output \HILO写入使能 ,
  output [1:0] OP_compare,
  output [1:0] \寄存器写入数据选择2位_alu_DM_PC_LO ,
  output JUMP,
  output Byte,
  output \有符号拓展结果选择 ,
  output [3:0] ALU_OP,
  output JR,
  output set,
  output [1:0] \写入寄存器选择2位_RT_RD_31号 ,
  output \DM写入使能 ,
  output Branch,
  output Systemcall
);

  wire ADD, ADDI, ADDIU, ADDU, AND, ANDI, BEQ, BLEZ, BNE, demultiplexer_1_out0, demultiplexer_1_out2,
       demultiplexer_1_out3, demultiplexer_1_out4, demultiplexer_1_out5, demultiplexer_1_out6,
       demultiplexer_1_out8, demultiplexer_1_out9, demultiplexer_1_out10, demultiplexer_1_out11,
       demultiplexer_1_out12, demultiplexer_1_out13, demultiplexer_2_out0, demultiplexer_2_out1,
       demultiplexer_2_out2, demultiplexer_2_out3, demultiplexer_2_out4, demultiplexer_2_out5,
       demultiplexer_2_out7, demultiplexer_2_out8, demultiplexer_2_out10, demultiplexer_2_out11,
       demultiplexer_2_out12, demultiplexer_2_out18, demultiplexer_2_out27, J, LW, MFLO, NOR, nor_1_out,
       not_1_out, not_2_out, OR, or_13_out, ORI, SLL, SLT, SLTI, SLTU, SRA, SRL, SUB;

  // Probe on OP
  // Probe on OP
  LED led_1 (.in(J));
  LED led_2 (.in(\写入寄存器选择2位_RT_RD_31号 [1]));
  LED led_3 (.in(BEQ));
  LED led_4 (.in(BNE));
  LED led_5 (.in(BLEZ));
  LED led_6 (.in(ADDI));
  LED led_7 (.in(ADDIU));
  LED led_8 (.in(SLTI));
  LED led_9 (.in(ANDI));
  LED led_10 (.in(ORI));
  LED led_11 (.in(Byte));
  LED led_12 (.in(LW));
  LED led_13 (.in(\DM写入使能 ));
  // Probe on OP
  // Probe on FUNC
  // Probe on FUNC
  // Probe on FUNC
  LED led_14 (.in(SLL));
  LED led_15 (.in(SRL));
  LED led_16 (.in(SRA));
  LED led_17 (.in(JR));
  LED led_18 (.in(Systemcall));
  LED led_19 (.in(MFLO));
  LED led_20 (.in(\HILO写入使能 ));
  LED led_21 (.in(ADD));
  LED led_22 (.in(ADDU));
  LED led_23 (.in(SUB));
  LED led_24 (.in(AND));
  LED led_25 (.in(OR));
  LED led_26 (.in(NOR));
  LED led_27 (.in(SLT));
  LED led_28 (.in(SLTU));
  // Probe on \写入寄存器选择2位_RT_RD_31号 
  // Probe on \寄存器写入数据选择2位_alu_DM_PC_LO 
  Demultiplexer #(.select(5), .disabled(0)) demultiplexer_1 (
    .out0(demultiplexer_1_out0), .out2(demultiplexer_1_out2), .out3(demultiplexer_1_out3),
    .out4(demultiplexer_1_out4), .out5(demultiplexer_1_out5), .out6(demultiplexer_1_out6),
    .out8(demultiplexer_1_out8), .out9(demultiplexer_1_out9), .out10(demultiplexer_1_out10),
    .out11(demultiplexer_1_out11), .out12(demultiplexer_1_out12), .out13(demultiplexer_1_out13), .in(1'b1),
    .sel(OP[4:0]));  // open: out1, out7, out14, out15, out16, out17, out18, out19, out20, out21, out22, out23, out24, out25, out26, out27, out28, out29, out30, out31, en
  Demultiplexer #(.select(5), .disabled(0)) demultiplexer_2 (
    .out0(demultiplexer_2_out0), .out1(demultiplexer_2_out1), .out2(demultiplexer_2_out2),
    .out3(demultiplexer_2_out3), .out4(demultiplexer_2_out4), .out5(demultiplexer_2_out5),
    .out7(demultiplexer_2_out7), .out8(demultiplexer_2_out8), .out10(demultiplexer_2_out10),
    .out11(demultiplexer_2_out11), .out12(demultiplexer_2_out12), .out18(demultiplexer_2_out18),
    .out27(demultiplexer_2_out27), .in(1'b1), .sel(FUNC[4:0]));  // open: out6, out9, out13, out14, out15, out16, out17, out19, out20, out21, out22, out23, out24, out25, out26, out28, out29, out30, out31, en
  nor nor_1 (nor_1_out, OP[0], OP[1], OP[2], OP[4], OP[5], OP[3]);
  not not_1 (not_1_out, OP[5]);
  not not_2 (not_2_out, FUNC[5]);
  // Probe on ALU_OP
  and _2 (J, demultiplexer_1_out2, not_1_out);
  and _3 (\写入寄存器选择2位_RT_RD_31号 [1], demultiplexer_1_out3, not_1_out);
  and _4 (BEQ, demultiplexer_1_out4, not_1_out);
  buf _5 (BNE, demultiplexer_1_out5);  // AND_Gate
  and _6 (BLEZ, demultiplexer_1_out6, not_1_out);
  and _8 (ADDI, demultiplexer_1_out8, not_1_out);
  and _9 (ADDIU, demultiplexer_1_out9, not_1_out);
  and _10 (SLTI, demultiplexer_1_out10, not_1_out);
  and _12 (ANDI, demultiplexer_1_out12, not_1_out);
  and _13 (ORI, demultiplexer_1_out13, not_1_out);
  // Probe on \ALU_SRC_2位_s_ext_RFD2_s_extun_0 
  and _32 (Byte, demultiplexer_1_out0, OP[5]);
  and _35 (LW, demultiplexer_1_out3, OP[5]);
  and _43 (\DM写入使能 , demultiplexer_1_out11, OP[5]);
  and _0 (SLL, demultiplexer_2_out0, nor_1_out, not_2_out);
  and _2_2 (SRL, demultiplexer_2_out2, nor_1_out, not_2_out);
  and _3_2 (SRA, demultiplexer_2_out3, nor_1_out, not_2_out);
  and _8_2 (JR, demultiplexer_2_out8, nor_1_out, not_2_out);
  and _12_2 (Systemcall, demultiplexer_2_out12, nor_1_out, not_2_out);
  and _18 (MFLO, demultiplexer_2_out18, nor_1_out, not_2_out);
  and _27 (\HILO写入使能 , demultiplexer_2_out27, nor_1_out, not_2_out);
  and _32_2 (ADD, demultiplexer_2_out0, nor_1_out, FUNC[5]);
  and _33 (ADDU, demultiplexer_2_out1, nor_1_out, FUNC[5]);
  and _34 (SUB, demultiplexer_2_out2, nor_1_out, FUNC[5]);
  and _36 (AND, demultiplexer_2_out4, nor_1_out, FUNC[5]);
  and _37 (OR, demultiplexer_2_out5, nor_1_out, FUNC[5]);
  and _39 (NOR, demultiplexer_2_out7, nor_1_out, FUNC[5]);
  and _42 (SLT, demultiplexer_2_out10, nor_1_out, FUNC[5]);
  and _43_2 (SLTU, demultiplexer_2_out11, nor_1_out, FUNC[5]);
  LED SPECAIL (.in(nor_1_out));
  or or_1 (\寄存器写入数据选择2位_alu_DM_PC_LO [1], \写入寄存器选择2位_RT_RD_31号 [1], MFLO);
  or or_2 (\寄存器写入数据选择2位_alu_DM_PC_LO [0], LW, MFLO, Byte);
  or or_3 (OP_compare[0], BNE, BLEZ);
  or or_4 (OP_compare[1], SLTI, SLTI, SLTU, BLEZ);
  or or_5 (JUMP, JR, J, \写入寄存器选择2位_RT_RD_31号 [1]);
  or or_6 (Branch, BEQ, BNE, BLEZ);
  or or_7 (\有符号拓展结果选择 , SRL, SRA, SLL);
  or or_8 (set, SLT, SLTI, SLTU);
  or or_9 (\写入寄存器选择2位_RT_RD_31号 [0], ADD, ADDU, AND, SLL, SRA, SRL, SUB, OR, NOR, SLT, SLTU, MFLO);
  or or_10 (\寄存器写入使能 , ADD, ADDI, ADDIU, ADDU, AND, ANDI, SLL, SRL, SRA, SUB, ORI, NOR, LW, \写入寄存器选择2位_RT_RD_31号 [1], Byte, MFLO, SLT, OR, SLTI, SLTU);
  or or_11 (\ALU_SRC_2位_s_ext_RFD2_s_extun_0 [0], ADD, ADDU, SUB, OR, NOR, SLT, SLTU, BEQ, BNE, \HILO写入使能 , BLEZ);
  or or_12 (\ALU_SRC_2位_s_ext_RFD2_s_extun_0 [1], ADDIU, BLEZ);
  or or_13 (or_13_out, BEQ, BNE, SLT, SLTI);
  or _0_2 (ALU_OP[0], or_13_out, AND, ANDI, ADD, ADDI, ADDIU, ADDU, \DM写入使能 , LW, NOR, SRA, Byte, BLEZ);
  or _2_3 (ALU_OP[1], SRL, BLEZ, SUB, or_13_out, AND, ANDI);
  or _2_4 (ALU_OP[2], \HILO写入使能 , Byte, LW, \DM写入使能 , SLTU, SUB, AND, ANDI, ADD, ADDI, ADDIU, ADDU);
  or _3_3 (ALU_OP[3], BLEZ, SLTU, or_13_out, NOR, ORI, OR);

  // Other names for the same wires on the sheet: ALU_SRC[1:0] = \ALU_SRC_2位_s_ext_RFD2_s_extun_0 ;
  //   EN_Register_write = \寄存器写入使能 ; ext_5or16 = \有符号拓展结果选择 ; DIVU = \HILO写入使能 ; HILO_wirte = \HILO写入使能 ;
  //   Jump_register = JR; LB = Byte; OP_cmp[1:0] = OP_compare; EN_DM = \DM写入使能 ; SW = \DM写入使能 ;
  //   写入寄存器选择[1:0] = \写入寄存器选择2位_RT_RD_31号 ; JAL = \写入寄存器选择2位_RT_RD_31号 [1];
  //   寄存器写入数据选择2位[1:0] = \寄存器写入数据选择2位_alu_DM_PC_LO 

  // Notes on the sheet:
  //   输入引脚区
  //   指令观察区
  //   输出引脚区
endmodule

module IF_ID (
  input  [31:0] PC,
  input  [31:0] instrution,
  input  T,
  input  enable,
  output [31:0] PC_out,
  output [31:0] ins_out
);

  // Probe on PC
  Register #(.width(32)) register_1 (.D(PC), .en(enable), .Q(PC_out), .clk(T));  // open: clr
  Register #(.width(32)) register_2 (.D(instrution), .en(enable), .Q(ins_out), .clk(T));  // open: clr
  // Probe on instrution

  // Other names for the same wires on the sheet: ins[31:0] = instrution; time = T
endmodule

module ID_EX (
  input  \byte ,
  input  B,
  input  DM_en,
  input  [1:0] op_compare,
  input  set,
  input  [31:0] _5or16,
  input  [1:0] data_in_re,
  input  [31:0] _16un,
  input  sys,
  input  [31:0] RFD1,
  input  [31:0] PC,
  input  [31:0] RFD2,
  input  [27:0] imme,
  input  we,
  input  [1:0] alu_src,
  input  [4:0] RW,
  input  [3:0] alu_op,
  input  JR,
  input  HILO,
  input  J,
  input  T,
  input  enable,
  output byte_out,
  output B_out,
  output DM_en_out,
  output [1:0] op_compare_out,
  output set_out,
  output [31:0] _5or16_out,
  output [1:0] data_in_re_out,
  output [31:0] _16un_out,
  output sys_out,
  output [31:0] RFD1_out,
  output [31:0] PC_out,
  output [31:0] RFD2_out,
  output [27:0] imme_out,
  output we_out,
  output [1:0] alu_src_out,
  output [4:0] RW_out,
  output [3:0] alu_op_out,
  output JR_out,
  output HILO_out,
  output J_out
);

  Register #(.width(1)) register_1 (.D(\byte ), .en(enable), .Q(byte_out), .clk(T));  // open: clr
  Register #(.width(1)) register_2 (.D(DM_en), .en(enable), .Q(DM_en_out), .clk(T));  // open: clr
  Register #(.width(1)) register_3 (.D(set), .en(enable), .Q(set_out), .clk(T));  // open: clr
  Register #(.width(2)) register_4 (.D(data_in_re), .en(enable), .Q(data_in_re_out), .clk(T));  // open: clr
  Register #(.width(1)) register_5 (.D(sys), .en(enable), .Q(sys_out), .clk(T));  // open: clr
  Register #(.width(32)) register_6 (.D(PC), .en(enable), .Q(PC_out), .clk(T));  // open: clr
  Register #(.width(28)) register_7 (.D(imme), .en(enable), .Q(imme_out), .clk(T));  // open: clr
  Register #(.width(2)) register_8 (.D(alu_src), .en(enable), .Q(alu_src_out), .clk(T));  // open: clr
  Register #(.width(4)) register_9 (.D(alu_op), .en(enable), .Q(alu_op_out), .clk(T));  // open: clr
  Register #(.width(1)) register_10 (.D(HILO), .en(enable), .Q(HILO_out), .clk(T));  // open: clr
  Register #(.width(1)) register_11 (.D(J), .en(enable), .Q(J_out), .clk(T));  // open: clr
  Register #(.width(1)) register_12 (.D(B), .en(enable), .Q(B_out), .clk(T));  // open: clr
  Register #(.width(2)) register_13 (.D(op_compare), .en(enable), .Q(op_compare_out), .clk(T));  // open: clr
  Register #(.width(32)) register_14 (.D(_5or16), .en(enable), .Q(_5or16_out), .clk(T));  // open: clr
  Register #(.width(32)) register_15 (.D(_16un), .en(enable), .Q(_16un_out), .clk(T));  // open: clr
  Register #(.width(32)) register_16 (.D(RFD1), .en(enable), .Q(RFD1_out), .clk(T));  // open: clr
  Register #(.width(32)) register_17 (.D(RFD2), .en(enable), .Q(RFD2_out), .clk(T));  // open: clr
  Register #(.width(1)) register_18 (.D(we), .en(enable), .Q(we_out), .clk(T));  // open: clr
  Register #(.width(5)) register_19 (.D(RW), .en(enable), .Q(RW_out), .clk(T));  // open: clr
  Register #(.width(1)) register_20 (.D(JR), .en(enable), .Q(JR_out), .clk(enable));  // open: clr
endmodule

module NPC (
  input  [31:0] _5or16,
  input  [27:0] imme,
  input  [31:0] PC,
  input  BRANCH,
  input  [31:0] RFD1,
  input  JUMP,
  input  JR,
  input  compare_result,
  output [31:0] PC_out,
  output branch_success
);

  wire [31:0] adder_1_out, adder_2_out, multiplexer_1_out, multiplexer_2_out, shifter_1_out;

  Adder #(.width(32)) adder_1 (.a(32'h4), .b(PC), .out(adder_1_out));  // open: cin, cout
  // Probe on imme
  Multiplexer #(.width(32), .disabled(0)) multiplexer_1 (
    .in0({adder_1_out[31:28], imme}), .in1(RFD1), .out(multiplexer_1_out), .sel(JR));  // open: en
  Shifter #(.width(32)) shifter_1 (.in(_5or16), .\dist (5'b00010), .out(shifter_1_out));
  Adder #(.width(32)) adder_2 (.a(adder_1_out), .b(shifter_1_out), .out(adder_2_out));  // open: cin, cout
  and and_1 (branch_success, BRANCH, compare_result);
  Multiplexer #(.width(32), .disabled(0)) multiplexer_2 (
    .in0(adder_1_out), .in1(adder_2_out), .out(multiplexer_2_out), .sel(branch_success));  // open: en
  Multiplexer #(.width(32), .disabled(0)) multiplexer_3 (
    .in0(multiplexer_2_out), .in1(multiplexer_1_out), .out(PC_out), .sel(JUMP));  // open: en

  // Other names for the same wires on the sheet: branch_succeed = branch_success
endmodule

module EX_MEM (
  input  WE,
  input  sys,
  input  [4:0] RW,
  input  in_4,
  input  \byte ,
  input  in_6,
  input  DM_en,
  input  [31:0] result,
  input  set,
  input  [31:0] RDF2,
  input  [1:0] data_in_re,
  input  [31:0] LO,
  input  [31:0] PC,
  input  enable,
  input  T,
  output WE_out,
  output sys_out,
  output [4:0] RW_out,
  output equal,
  output byte_out,
  output lower,
  output DM_en_out,
  output [31:0] result_out,
  output set_out,
  output [31:0] RDF2_out,
  output [1:0] data_in_re_out,
  output [31:0] LO_out,
  output [31:0] PC_out
);

  Register #(.width(1)) register_1 (.D(WE), .en(enable), .Q(WE_out), .clk(T));  // open: clr
  Register #(.width(5)) register_2 (.D(RW), .en(enable), .Q(RW_out), .clk(T));  // open: clr
  Register #(.width(1)) register_3 (.D(\byte ), .en(enable), .Q(byte_out), .clk(T));  // open: clr
  Register #(.width(1)) register_4 (.D(DM_en), .en(enable), .Q(DM_en_out), .clk(T));  // open: clr
  Register #(.width(1)) register_5 (.D(set), .en(enable), .Q(set_out), .clk(T));  // open: clr
  Register #(.width(2)) register_6 (.D(data_in_re), .en(enable), .Q(data_in_re_out), .clk(T));  // open: clr
  Register #(.width(32)) register_7 (.D(PC), .en(enable), .Q(PC_out), .clk(T));  // open: clr
  Register #(.width(1)) register_8 (.D(sys), .en(enable), .Q(sys_out), .clk(T));  // open: clr
  Register #(.width(1)) register_9 (.D(in_4), .en(enable), .Q(equal), .clk(T));  // open: clr
  Register #(.width(1)) register_10 (.D(in_6), .en(enable), .Q(lower), .clk(T));  // open: clr
  Register #(.width(32)) register_11 (.D(result), .en(enable), .Q(result_out), .clk(T));  // open: clr
  Register #(.width(32)) register_12 (.D(RDF2), .en(enable), .Q(RDF2_out), .clk(T));  // open: clr
  Register #(.width(32)) register_13 (.D(LO), .en(enable), .Q(LO_out), .clk(T));  // open: clr
endmodule

module MEM_RB (
  input  [1:0] sel,
  input  sys,
  input  WE,
  input  in_4,
  input  [4:0] RW,
  input  in_6,
  input  \byte ,
  input  [31:0] result,
  input  set,
  input  [31:0] LO,
  input  [1:0] data_in_re,
  input  [31:0] PC,
  input  [31:0] data,
  input  in_14,
  input  T,
  output [1:0] sel_out,
  output sys_out,
  output WE_out,
  output equal,
  output [4:0] RW_out,
  output lower,
  output byte_out,
  output [31:0] result_out,
  output set_out,
  output [31:0] LO_out,
  output [1:0] data_in_re_out,
  output [31:0] PC_out,
  output [31:0] data_out
);

  Register #(.width(2)) register_1 (.D(sel), .en(in_14), .Q(sel_out), .clk(T));  // open: clr
  Register #(.width(1)) register_2 (.D(WE), .en(in_14), .Q(WE_out), .clk(T));  // open: clr
  Register #(.width(5)) register_3 (.D(RW), .en(in_14), .Q(RW_out), .clk(T));  // open: clr
  Register #(.width(1)) register_4 (.D(\byte ), .en(in_14), .Q(byte_out), .clk(T));  // open: clr
  Register #(.width(1)) register_5 (.D(set), .en(in_14), .Q(set_out), .clk(T));  // open: clr
  Register #(.width(2)) register_6 (.D(data_in_re), .en(in_14), .Q(data_in_re_out), .clk(T));  // open: clr
  Register #(.width(32)) register_7 (.D(PC), .en(in_14), .Q(PC_out), .clk(T));  // open: clr
  Register #(.width(1)) register_8 (.D(sys), .en(in_14), .Q(sys_out), .clk(T));  // open: clr
  Register #(.width(1)) register_9 (.D(in_4), .en(in_14), .Q(equal), .clk(T));  // open: clr
  Register #(.width(1)) register_10 (.D(in_6), .en(in_14), .Q(lower), .clk(T));  // open: clr
  Register #(.width(32)) register_11 (.D(result), .en(in_14), .Q(result_out), .clk(T));  // open: clr
  Register #(.width(32)) register_12 (.D(LO), .en(in_14), .Q(LO_out), .clk(T));  // open: clr
  Register #(.width(32)) register_13 (.D(data), .en(in_14), .Q(data_out), .clk(T));  // open: clr
endmodule
